// Logisim project Final.circ as structural Verilog: 1 circuit, main circuit main
module main (
  input  in_1,
  output out_2
);

  wire and_1_out, and_2_out, clock_1_out, clock_2_out, clock_3_out, d_ff_1_qn, j_k_ff_1_q, j_k_ff_1_qn,
       j_k_ff_2_q, j_k_ff_2_qn, or_1_out, xor_1_out;

  Clock clock_1 (.out(clock_1_out));
  xor xor_1 (xor_1_out, in_1, or_1_out);
  or or_1 (or_1_out, j_k_ff_1_qn, and_1_out);
  J_K_Flip_Flop j_k_ff_1 (
    .J(in_1), .clk(clock_1_out), .K(xor_1_out), .Q(j_k_ff_1_q), .Qn(j_k_ff_1_qn), .preset(1'b0), .reset(1'b0));  // open: en
  Clock clock_2 (.out(clock_2_out));
  and and_1 (and_1_out, j_k_ff_2_qn, d_ff_1_qn);
  J_K_Flip_Flop j_k_ff_2 (
    .J(j_k_ff_1_q), .clk(clock_2_out), .K(j_k_ff_1_q), .Q(j_k_ff_2_q), .Qn(j_k_ff_2_qn), .preset(1'b0),
    .reset(1'b0));  // open: en
  Clock clock_3 (.out(clock_3_out));
  and and_2 (and_2_out, j_k_ff_1_q, j_k_ff_2_q);
  D_Flip_Flop d_ff_1 (
    .clk(clock_3_out), .D(and_2_out), .Q(out_2), .Qn(d_ff_1_qn), .preset(1'b0), .reset(1'b0));  // open: en
  // Probe on out_2
endmodule
