// Logisim project Final2.circ as structural Verilog: 7 circuits, main circuit main
module main (
  input  A,
  input  B
);

  wire clock_1_out, d0_1_d0, d1_1_d1, d2_1_d2, d_ff_1_q, d_ff_2_q, d_ff_3_q;

  D0 d0_1 (.A(A), .B(B), .Q0(d_ff_1_q), .Q1(d_ff_2_q), .Q2(d_ff_3_q), .D0(d0_1_d0));
  D1 d1_1 (.A(A), .B(B), .Q0(d_ff_1_q), .Q1(d_ff_2_q), .Q2(d_ff_3_q), .D1(d1_1_d1));
  D2 d2_1 (.A(A), .B(B), .Q0(d_ff_1_q), .Q1(d_ff_2_q), .Q2(d_ff_3_q), .D2(d2_1_d2));
  Clock clock_1 (.out(clock_1_out));
  D_Flip_Flop d_ff_1 (.clk(clock_1_out), .D(d0_1_d0), .Q(d_ff_1_q));  // open: Qn, preset, en, reset
  D_Flip_Flop d_ff_2 (.clk(clock_1_out), .D(d1_1_d1), .Q(d_ff_2_q));  // open: Qn, preset, en, reset
  D_Flip_Flop d_ff_3 (.clk(clock_1_out), .D(d2_1_d2), .Q(d_ff_3_q));  // open: Qn, preset, en, reset
endmodule

module D0 (
  input  A,
  input  B,
  input  Q0,
  input  Q1,
  input  Q2,
  output D0
);

  wire and_1_out, and_2_out, and_3_out, and_4_out, and_5_out, and_6_out, and_7_out, and_8_out, not_1_out,
       not_2_out, not_3_out, not_4_out, not_5_out, not_6_out, not_7_out, not_8_out, not_9_out, not_10_out,
       not_11_out, not_12_out, not_13_out, not_14_out, not_15_out, not_16_out, not_17_out;

  not not_1 (not_1_out, Q2);
  not not_2 (not_2_out, Q1);
  not not_3 (not_3_out, Q0);
  not not_4 (not_4_out, Q0);
  not not_5 (not_5_out, B);
  not not_6 (not_6_out, Q2);
  not not_7 (not_7_out, Q0);
  not not_8 (not_8_out, Q2);
  not not_9 (not_9_out, Q0);
  not not_10 (not_10_out, A);
  not not_11 (not_11_out, A);
  not not_12 (not_12_out, Q0);
  not not_13 (not_13_out, A);
  not not_14 (not_14_out, Q2);
  not not_15 (not_15_out, Q1);
  not not_16 (not_16_out, A);
  not not_17 (not_17_out, B);
  and and_1 (and_1_out, not_1_out, not_2_out, not_3_out);
  and and_2 (and_2_out, not_4_out, A, not_5_out);
  and and_3 (and_3_out, not_6_out, Q0, A, B);
  and and_4 (and_4_out, Q2, Q1, not_7_out, B);
  and and_5 (and_5_out, not_8_out, not_9_out, not_10_out);
  and and_6 (and_6_out, Q2, Q1, Q0, not_11_out);
  and and_7 (and_7_out, not_12_out, not_13_out, B);
  and and_8 (and_8_out, not_14_out, not_15_out, not_16_out, not_17_out);
  or or_1 (D0, and_1_out, and_2_out, and_3_out, and_4_out, and_5_out, and_6_out, and_7_out, and_8_out);
endmodule

module D1 (
  input  A,
  input  B,
  input  Q0,
  input  Q1,
  input  Q2,
  output D1
);

  wire and_1_out, and_2_out, and_3_out, and_4_out, and_5_out, and_6_out, and_7_out, not_1_out, not_2_out,
       not_3_out, not_4_out, not_5_out, not_6_out, not_7_out, not_8_out, not_9_out, not_10_out, not_11_out,
       not_12_out;

  not not_1 (not_1_out, Q1);
  not not_2 (not_2_out, A);
  not not_3 (not_3_out, Q0);
  not not_4 (not_4_out, Q1);
  not not_5 (not_5_out, Q0);
  not not_6 (not_6_out, B);
  not not_7 (not_7_out, Q2);
  not not_8 (not_8_out, Q1);
  not not_9 (not_9_out, Q2);
  not not_10 (not_10_out, Q0);
  not not_11 (not_11_out, A);
  not not_12 (not_12_out, B);
  and and_1 (and_1_out, not_1_out, Q0, not_2_out);
  and and_2 (and_2_out, Q1, not_3_out, B);
  and and_3 (and_3_out, Q2, Q1, B);
  and and_4 (and_4_out, not_4_out, not_5_out, A, not_6_out);
  and and_5 (and_5_out, not_7_out, not_8_out, Q0, B);
  and and_6 (and_6_out, not_9_out, Q1, not_10_out, not_11_out);
  and and_7 (and_7_out, Q1, Q0, A, not_12_out);
  or or_1 (D1, and_1_out, and_2_out, and_3_out, and_4_out, and_5_out, and_6_out, and_7_out);
endmodule

module D2 (
  input  A,
  input  B,
  input  Q0,
  input  Q1,
  input  Q2,
  output D2
);

  wire and_1_out, and_2_out, and_3_out, and_4_out, and_5_out, and_6_out, and_7_out, and_8_out, and_9_out,
       and_10_out, not_1_out, not_2_out, not_3_out, not_4_out, not_5_out, not_6_out, not_7_out, not_8_out,
       not_9_out, not_10_out, not_11_out, not_12_out, not_13_out, not_14_out, not_15_out, not_16_out;

  not not_1 (not_1_out, Q1);
  not not_2 (not_2_out, A);
  not not_3 (not_3_out, Q2);
  not not_4 (not_4_out, Q2);
  not not_5 (not_5_out, Q2);
  not not_6 (not_6_out, Q1);
  not not_7 (not_7_out, B);
  not not_8 (not_8_out, A);
  not not_9 (not_9_out, Q2);
  not not_10 (not_10_out, Q1);
  not not_11 (not_11_out, Q0);
  not not_12 (not_12_out, B);
  not not_13 (not_13_out, Q2);
  not not_14 (not_14_out, Q1);
  not not_15 (not_15_out, A);
  not not_16 (not_16_out, B);
  and and_1 (and_1_out, Q2, not_1_out, B);
  and and_2 (and_2_out, Q2, not_2_out, B);
  and and_3 (and_3_out, not_3_out, Q0, A, B);
  and and_4 (and_4_out, not_4_out, Q1, A, B);
  and and_5 (and_5_out, not_5_out, Q1, Q0, B);
  and and_6 (and_6_out, Q2, not_6_out, Q0, A);
  and and_7 (and_7_out, Q2, Q1, A, not_7_out);
  and and_8 (and_8_out, Q2, Q1, Q0, not_8_out);
  and and_9 (and_9_out, not_9_out, not_10_out, not_11_out, A, not_12_out);
  and and_10 (and_10_out, not_13_out, not_14_out, Q0, not_15_out, not_16_out);
  or or_1 (D2, and_1_out, and_2_out, and_3_out, and_4_out, and_5_out, and_6_out, and_7_out, and_8_out, and_9_out, and_10_out);
endmodule

module D0_1 (
  input  A,
  input  B,
  input  Q2,
  input  Q1,
  input  Q0,
  output D0
);

  wire and_1_out, and_2_out, and_3_out, and_4_out, and_5_out, and_6_out, not_1_out, not_2_out, not_3_out,
       not_4_out, not_5_out;

  not not_1 (not_1_out, A);
  not not_2 (not_2_out, B);
  not not_3 (not_3_out, Q2);
  not not_4 (not_4_out, Q1);
  not not_5 (not_5_out, Q0);
  and and_1 (and_1_out, not_1_out, not_2_out, not_4_out, not_3_out);
  and and_2 (and_2_out, not_1_out, not_4_out, not_5_out);
  and and_3 (and_3_out, not_1_out, Q1, not_5_out);
  and and_4 (and_4_out, A, not_2_out, not_5_out);
  and and_5 (and_5_out, Q2, Q1, Q0);
  and and_6 (and_6_out, A, B, not_3_out, Q0);
  or or_1 (D0, and_2_out, and_3_out, and_4_out, and_5_out, and_6_out, and_1_out);
endmodule

module D1_1 (
  input  A,
  input  B,
  input  Q2,
  input  Q1,
  input  Q0,
  output D1
);

  wire and_1_out, and_2_out, and_3_out, and_4_out, and_5_out, and_6_out, not_1_out, not_2_out, not_3_out,
       not_4_out, not_5_out;

  not not_1 (not_1_out, A);
  not not_2 (not_2_out, B);
  not not_3 (not_3_out, Q2);
  not not_4 (not_4_out, Q1);
  not not_5 (not_5_out, Q0);
  and and_1 (and_1_out, not_2_out, not_3_out, Q1, Q0);
  and and_2 (and_2_out, not_1_out, Q0);
  and and_3 (and_3_out, B, Q2, Q1);
  and and_4 (and_4_out, A, B, Q1, not_5_out);
  and and_5 (and_5_out, A, not_2_out, not_4_out, not_5_out);
  and and_6 (and_6_out, A, B, not_3_out, not_4_out);
  or or_1 (D1, and_2_out, and_3_out, and_4_out, and_5_out, and_6_out, and_1_out);
endmodule

module D2_1 (
  input  A,
  input  B,
  input  Q2,
  input  Q1,
  input  Q0
);

  wire and_1_out, and_2_out, and_3_out, and_4_out, and_6_out, and_7_out, and_8_out, and_9_out, not_1_out,
       not_2_out, not_3_out, not_4_out, not_5_out;

  not not_1 (not_1_out, A);
  not not_2 (not_2_out, B);
  not not_3 (not_3_out, Q2);
  not not_4 (not_4_out, Q1);
  not not_5 (not_5_out, Q0);
  and and_1 (and_1_out, A, not_2_out, not_3_out, not_4_out, not_5_out);
  and and_2 (and_2_out, not_1_out, B, Q1, Q0);
  and and_3 (and_3_out, not_1_out, Q2, Q1, Q0);
  and and_4 (and_4_out, not_1_out, not_2_out, not_4_out, not_3_out, Q0);
  // AND_Gate and_5 has open pins: in0=not_1_out, in1=B, in2=Q2, out=open
  and and_6 (and_6_out, A, B, not_3_out);
  and and_7 (and_7_out, A, B, not_4_out);
  and and_8 (and_8_out, A, not_2_out, Q2, Q1);
  and and_9 (and_9_out, A, Q2, not_4_out, Q0);
endmodule
