// Logisim project HW#6.circ as structural Verilog: 6 circuits, main circuit main
module main (
  output A,
  output A_2,
  output A_3,
  output A_4,
  output B,
  output B_2,
  output C,
  output B_3,
  output C_2,
  output C_3,
  output D,
  output B_4,
  output D_2,
  output E,
  output D_3,
  output E_2,
  output F,
  output C_4,
  output F_2,
  output G,
  output E_3,
  output G_2,
  output F_3,
  output D_4,
  output G_3,
  output E_4,
  output F_4,
  output G_4
);

  wire and_1_out, and_2_out, and_3_out, and_4_out, and_5_out, and_6_out, and_7_out, and_8_out, and_9_out,
       and_10_out, and_11_out, and_12_out, and_13_out, and_14_out, and_15_out, and_16_out, and_17_out,
       and_18_out, and_19_out, and_20_out, and_21_out, and_22_out, and_23_out, and_24_out, and_25_out,
       and_26_out, and_27_out, and_28_out, and_29_out, and_30_out, and_31_out, and_32_out, and_33_out,
       and_34_out, and_35_out, and_36_out, and_37_out, and_38_out, and_39_out, and_40_out, and_41_out,
       and_42_out, and_43_out, and_44_out, and_45_out, and_46_out, and_47_out, and_48_out, and_49_out,
       and_50_out, and_51_out, and_52_out, and_53_out, and_54_out, and_55_out, and_56_out, and_57_out,
       and_58_out, and_59_out, and_60_out, and_61_out, and_62_out, and_63_out, and_64_out, and_65_out,
       and_66_out, and_67_out, and_68_out, and_69_out, and_70_out, and_71_out, and_72_out, and_73_out,
       and_74_out, and_75_out, and_76_out, and_77_out, and_78_out, and_79_out, and_80_out, and_81_out,
       and_82_out, and_83_out, and_84_out, and_85_out, and_86_out, and_87_out, and_88_out, clock_1_out,
       d_ff_1_q, d_ff_1_qn, d_ff_2_q, d_ff_2_qn, d_ff_3_q, d_ff_3_qn, d_ff_4_q, d_ff_4_qn, nand_1_out,
       nand_2_out, nand_3_out, nand_4_out, nand_5_out, nand_6_out, nand_7_out, nand_8_out, nand_9_out,
       nand_10_out, nand_11_out, nand_12_out, nand_13_out, nand_14_out, nand_15_out, nand_16_out,
       nand_17_out, nand_18_out, nand_19_out, nand_20_out, nand_21_out, nand_22_out, nand_23_out,
       nand_24_out, nand_25_out, nand_26_out, nand_27_out, nand_28_out, nand_29_out, nand_30_out,
       nand_31_out, nand_32_out, nand_33_out, nand_34_out, nand_35_out, nand_36_out, nand_37_out,
       nand_38_out, nand_39_out, nand_40_out, nand_41_out, nand_42_out, nand_43_out, nand_44_out,
       nand_45_out, nand_46_out, nand_47_out, nand_48_out, nand_49_out, nand_50_out, nand_51_out,
       nand_52_out, nand_53_out, nand_54_out, nand_55_out, nand_56_out, nand_57_out, nand_58_out,
       nand_59_out, nand_60_out, nand_61_out, nand_62_out, nand_63_out, nand_64_out, nand_65_out,
       nand_66_out, nand_67_out, nand_68_out, nand_69_out, nand_70_out, nand_71_out, nand_72_out,
       nand_73_out, nand_74_out, nand_75_out, nand_76_out, nand_77_out, nand_78_out, nand_79_out,
       nand_80_out, nand_81_out, nand_82_out, nand_83_out, nand_84_out, nand_85_out, nand_86_out,
       nand_87_out, not_1_out, not_2_out, not_3_out, not_4_out, not_5_out, not_6_out, not_7_out, not_8_out,
       not_9_out, not_10_out, not_11_out, not_12_out, not_13_out, not_14_out, not_15_out, not_16_out,
       not_17_out, not_18_out, not_19_out, not_20_out, not_21_out, not_22_out, not_23_out, not_24_out,
       not_25_out, not_26_out, not_27_out, not_28_out, not_29_out, not_30_out, not_31_out, not_32_out,
       not_33_out, not_34_out, not_35_out, not_36_out, not_37_out, not_38_out, not_39_out, not_40_out,
       not_41_out, not_42_out, not_43_out, not_44_out, not_45_out, not_46_out, not_47_out, not_48_out,
       not_49_out, not_50_out, not_51_out, not_52_out, not_53_out, not_54_out, not_55_out, not_56_out,
       not_57_out, not_58_out, not_59_out, not_60_out, not_61_out, not_62_out, not_63_out, not_64_out,
       not_65_out, not_66_out, not_67_out, not_68_out, not_69_out, not_70_out, not_71_out, not_72_out,
       not_73_out, not_74_out, not_75_out, not_76_out, not_77_out, not_78_out, not_79_out, not_80_out,
       not_81_out, not_82_out, not_83_out, not_84_out, not_85_out, not_86_out, not_87_out, not_88_out,
       not_89_out, not_90_out, not_91_out, not_92_out, not_93_out, not_94_out, not_95_out, not_96_out,
       not_97_out, not_98_out, not_99_out, not_100_out, not_101_out, not_102_out, not_103_out, not_104_out,
       not_105_out, not_106_out, not_107_out, not_108_out, not_109_out, not_110_out, not_111_out,
       not_112_out, not_113_out, not_114_out, not_115_out, not_116_out, not_117_out, not_118_out;

  Clock clock_1 (.out(clock_1_out));
  D_Flip_Flop d_ff_1 (.clk(clock_1_out), .D(d_ff_1_qn), .Q(d_ff_1_q), .Qn(d_ff_1_qn));  // open: preset, en, reset
  D_Flip_Flop d_ff_2 (.clk(d_ff_1_qn), .D(d_ff_2_qn), .Q(d_ff_2_q), .Qn(d_ff_2_qn));  // open: preset, en, reset
  D_Flip_Flop d_ff_3 (.clk(d_ff_2_qn), .D(d_ff_3_qn), .Q(d_ff_3_q), .Qn(d_ff_3_qn));  // open: preset, en, reset
  D_Flip_Flop d_ff_4 (.clk(d_ff_3_qn), .D(d_ff_4_qn), .Q(d_ff_4_q), .Qn(d_ff_4_qn));  // open: preset, en, reset
  nand nand_1 (nand_1_out, d_ff_4_q, d_ff_4_q);
  nand nand_2 (nand_2_out, d_ff_3_q, d_ff_3_q);
  nand nand_3 (nand_3_out, d_ff_2_q, d_ff_2_q);
  nand nand_4 (nand_4_out, d_ff_4_q, d_ff_4_q);
  nand nand_5 (nand_5_out, d_ff_1_q, d_ff_1_q);
  nand nand_6 (nand_6_out, d_ff_1_q, d_ff_1_q);
  nand nand_7 (nand_7_out, d_ff_4_q, d_ff_4_q);
  nand nand_8 (nand_8_out, d_ff_3_q, d_ff_3_q);
  nand nand_9 (nand_9_out, d_ff_2_q, d_ff_2_q);
  nand nand_10 (nand_10_out, d_ff_4_q, d_ff_4_q);
  nand nand_11 (nand_11_out, d_ff_3_q, d_ff_3_q);
  nand nand_12 (nand_12_out, d_ff_4_q, d_ff_4_q);
  nand nand_13 (nand_13_out, d_ff_3_q, d_ff_3_q);
  nand nand_14 (nand_14_out, d_ff_2_q, d_ff_2_q);
  nand nand_15 (nand_15_out, d_ff_1_q, d_ff_1_q);
  nand nand_16 (nand_16_out, d_ff_2_q, d_ff_2_q);
  nand nand_17 (nand_17_out, d_ff_1_q, d_ff_1_q);
  nand nand_18 (nand_18_out, d_ff_4_q, d_ff_4_q);
  nand nand_19 (nand_19_out, d_ff_2_q, d_ff_2_q);
  nand nand_20 (nand_20_out, d_ff_1_q, d_ff_1_q);
  nand nand_21 (nand_21_out, d_ff_1_q, d_ff_1_q);
  nand nand_22 (nand_22_out, d_ff_4_q, d_ff_4_q);
  nand nand_23 (nand_23_out, d_ff_3_q, d_ff_3_q);
  nand nand_24 (nand_24_out, d_ff_1_q, d_ff_1_q);
  nand nand_25 (nand_25_out, d_ff_3_q, d_ff_3_q);
  nand nand_26 (nand_26_out, d_ff_2_q, d_ff_2_q);
  nand nand_27 (nand_27_out, d_ff_2_q, d_ff_2_q);
  nand nand_28 (nand_28_out, d_ff_1_q, d_ff_1_q);
  nand nand_29 (nand_29_out, d_ff_2_q, d_ff_2_q);
  nand nand_30 (nand_30_out, d_ff_3_q, d_ff_3_q);
  nand nand_31 (nand_31_out, d_ff_1_q, d_ff_1_q);
  nand nand_32 (nand_32_out, d_ff_4_q, d_ff_4_q);
  nand nand_33 (nand_33_out, d_ff_1_q, d_ff_1_q);
  nand nand_34 (nand_34_out, d_ff_3_q, d_ff_3_q);
  nand nand_35 (nand_35_out, d_ff_2_q, d_ff_2_q);
  nand nand_36 (nand_36_out, d_ff_1_q, d_ff_1_q);
  nand nand_37 (nand_37_out, d_ff_4_q, d_ff_4_q);
  nand nand_38 (nand_38_out, d_ff_2_q, d_ff_2_q);
  nand nand_39 (nand_39_out, d_ff_3_q, d_ff_3_q);
  nand nand_40 (nand_40_out, d_ff_3_q, d_ff_3_q);
  nand nand_41 (nand_41_out, d_ff_2_q, d_ff_2_q);
  nand nand_42 (nand_42_out, d_ff_1_q, d_ff_1_q);
  nand nand_43 (nand_43_out, d_ff_4_q, d_ff_4_q);
  nand nand_44 (nand_44_out, d_ff_4_q, d_ff_4_q);
  nand nand_45 (nand_45_out, d_ff_3_q, d_ff_3_q);
  nand nand_46 (nand_46_out, d_ff_2_q, d_ff_2_q);
  nand nand_47 (nand_47_out, d_ff_4_q, d_ff_4_q);
  nand nand_48 (nand_48_out, d_ff_3_q, d_ff_3_q);
  nand nand_49 (nand_49_out, d_ff_1_q, d_ff_1_q);
  nand nand_50 (nand_50_out, d_ff_4_q, d_ff_4_q);
  nand nand_51 (nand_51_out, d_ff_3_q, d_ff_3_q);
  nand nand_52 (nand_52_out, d_ff_2_q, d_ff_2_q);
  nand nand_53 (nand_53_out, nand_1_out, nand_2_out, nand_3_out);
  nand nand_54 (nand_54_out, nand_4_out, nand_5_out);
  nand nand_55 (nand_55_out, d_ff_3_q, nand_6_out);
  nand nand_56 (nand_56_out, nand_7_out, d_ff_3_q, d_ff_2_q);
  nand nand_57 (nand_57_out, d_ff_4_q, nand_8_out, d_ff_2_q, d_ff_1_q);
  nand nand_58 (nand_58_out, d_ff_4_q, d_ff_3_q, nand_9_out);
  nand nand_59 (nand_59_out, nand_10_out, nand_11_out, d_ff_2_q);
  nand nand_60 (nand_60_out, nand_12_out, d_ff_2_q, d_ff_1_q);
  nand nand_61 (nand_61_out, nand_13_out, d_ff_2_q, d_ff_1_q);
  nand nand_62 (nand_62_out, d_ff_3_q, nand_14_out, nand_15_out);
  nand nand_63 (nand_63_out, d_ff_4_q, d_ff_3_q, nand_16_out);
  nand nand_64 (nand_64_out, d_ff_4_q, d_ff_3_q, nand_17_out);
  nand nand_65 (nand_65_out, nand_18_out, d_ff_2_q, d_ff_1_q);
  nand nand_66 (nand_66_out, d_ff_3_q, nand_19_out, nand_20_out);
  nand nand_67 (nand_67_out, d_ff_4_q, d_ff_3_q, nand_21_out);
  nand nand_68 (nand_68_out, nand_22_out, nand_23_out, nand_24_out);
  nand nand_69 (nand_69_out, nand_25_out, nand_26_out);
  nand nand_70 (nand_70_out, nand_27_out, nand_28_out);
  nand nand_71 (nand_71_out, d_ff_4_q, nand_29_out);
  nand nand_72 (nand_72_out, d_ff_4_q, nand_30_out, d_ff_1_q);
  nand nand_73 (nand_73_out, d_ff_4_q, d_ff_3_q, nand_31_out);
  nand nand_74 (nand_74_out, nand_32_out, nand_33_out);
  nand nand_75 (nand_75_out, nand_34_out, nand_35_out);
  nand nand_76 (nand_76_out, d_ff_3_q, nand_36_out);
  nand nand_77 (nand_77_out, nand_37_out, d_ff_3_q, d_ff_2_q);
  nand nand_78 (nand_78_out, d_ff_4_q, nand_38_out);
  nand nand_79 (nand_79_out, d_ff_4_q, nand_39_out, d_ff_1_q);
  nand nand_80 (nand_80_out, nand_40_out, nand_41_out);
  nand nand_81 (nand_81_out, d_ff_3_q, nand_42_out);
  nand nand_82 (nand_82_out, nand_43_out, d_ff_3_q, d_ff_2_q);
  nand nand_83 (nand_83_out, nand_44_out, nand_45_out, nand_46_out);
  nand nand_84 (nand_84_out, nand_47_out, nand_48_out, nand_49_out);
  nand nand_85 (nand_85_out, nand_50_out, d_ff_3_q, d_ff_2_q);
  nand nand_86 (nand_86_out, d_ff_4_q, nand_51_out, d_ff_2_q, d_ff_1_q);
  nand nand_87 (nand_87_out, d_ff_4_q, d_ff_3_q, nand_52_out, d_ff_1_q);
  nand nand_88 (C_4, nand_65_out, nand_66_out, nand_67_out);
  nand nand_89 (F_4, nand_80_out, nand_81_out, nand_82_out);
  nand nand_90 (A_4, nand_53_out, nand_54_out, nand_55_out, nand_56_out, nand_57_out, nand_58_out);
  nand nand_91 (B_4, nand_59_out, nand_60_out, nand_61_out, nand_62_out, nand_63_out, nand_64_out);
  nand nand_92 (D_4, nand_68_out, nand_69_out, nand_70_out, nand_71_out, nand_72_out, nand_73_out);
  nand nand_93 (E_4, nand_74_out, nand_75_out, nand_76_out, nand_77_out, nand_78_out, nand_79_out);
  nand nand_94 (G_4, nand_83_out, nand_84_out, nand_85_out, nand_86_out, nand_87_out);
  _7_Segment_Display u_7_segment_display_1 (.g(G_4), .f(F_4), .a(A_4), .b(B_4), .e(E_4), .d(D_4), .c(C_4));  // open: dp
  not not_1 (not_1_out, d_ff_4_q);
  not not_2 (not_2_out, d_ff_3_q);
  not not_3 (not_3_out, d_ff_2_q);
  not not_4 (not_4_out, d_ff_4_q);
  not not_5 (not_5_out, d_ff_3_q);
  not not_6 (not_6_out, d_ff_4_q);
  not not_7 (not_7_out, d_ff_2_q);
  not not_8 (not_8_out, d_ff_4_q);
  not not_9 (not_9_out, d_ff_1_q);
  not not_10 (not_10_out, d_ff_3_q);
  not not_11 (not_11_out, d_ff_2_q);
  not not_12 (not_12_out, d_ff_4_q);
  not not_13 (not_13_out, d_ff_3_q);
  not not_14 (not_14_out, d_ff_4_q);
  not not_15 (not_15_out, d_ff_1_q);
  not not_16 (not_16_out, d_ff_3_q);
  not not_17 (not_17_out, d_ff_2_q);
  not not_18 (not_18_out, d_ff_4_q);
  not not_19 (not_19_out, d_ff_1_q);
  not not_20 (not_20_out, d_ff_3_q);
  not not_21 (not_21_out, d_ff_2_q);
  not not_22 (not_22_out, d_ff_4_q);
  not not_23 (not_23_out, d_ff_3_q);
  not not_24 (not_24_out, d_ff_2_q);
  not not_25 (not_25_out, d_ff_3_q);
  not not_26 (not_26_out, d_ff_1_q);
  not not_27 (not_27_out, d_ff_2_q);
  not not_28 (not_28_out, d_ff_3_q);
  not not_29 (not_29_out, d_ff_2_q);
  not not_30 (not_30_out, d_ff_1_q);
  not not_31 (not_31_out, d_ff_4_q);
  not not_32 (not_32_out, d_ff_4_q);
  not not_33 (not_33_out, d_ff_2_q);
  not not_34 (not_34_out, d_ff_1_q);
  not not_35 (not_35_out, d_ff_3_q);
  not not_36 (not_36_out, d_ff_3_q);
  not not_37 (not_37_out, d_ff_2_q);
  not not_38 (not_38_out, d_ff_1_q);
  not not_39 (not_39_out, d_ff_4_q);
  not not_40 (not_40_out, d_ff_4_q);
  not not_41 (not_41_out, d_ff_3_q);
  not not_42 (not_42_out, d_ff_2_q);
  not not_43 (not_43_out, d_ff_4_q);
  not not_44 (not_44_out, d_ff_2_q);
  not not_45 (not_45_out, d_ff_4_q);
  not not_46 (not_46_out, d_ff_1_q);
  not not_47 (not_47_out, d_ff_3_q);
  not not_48 (not_48_out, d_ff_1_q);
  not not_49 (not_49_out, d_ff_2_q);
  not not_50 (not_50_out, d_ff_1_q);
  and and_1 (and_1_out, not_1_out, not_2_out, not_3_out);
  and and_2 (and_2_out, not_4_out, not_5_out, d_ff_1_q);
  and and_3 (and_3_out, not_6_out, not_7_out, d_ff_1_q);
  and and_4 (and_4_out, not_8_out, d_ff_3_q, d_ff_2_q, not_9_out);
  and and_5 (and_5_out, d_ff_4_q, not_10_out, d_ff_2_q);
  and and_6 (and_6_out, d_ff_4_q, d_ff_3_q, not_11_out);
  and and_7 (and_7_out, d_ff_4_q, d_ff_3_q, d_ff_1_q);
  and and_8 (and_8_out, not_12_out, not_13_out, d_ff_1_q);
  and and_9 (and_9_out, not_14_out, d_ff_2_q, not_15_out);
  and and_10 (and_10_out, not_16_out, d_ff_2_q);
  and and_11 (and_11_out, d_ff_4_q, d_ff_3_q, not_17_out);
  and and_12 (and_12_out, not_18_out, d_ff_2_q, not_19_out);
  and and_13 (and_13_out, not_20_out, d_ff_2_q, d_ff_1_q);
  and and_14 (and_14_out, d_ff_4_q, d_ff_3_q, not_21_out, d_ff_1_q);
  and and_15 (and_15_out, not_22_out, not_23_out, not_24_out);
  and and_16 (and_16_out, d_ff_2_q, d_ff_1_q);
  and and_17 (and_17_out, d_ff_4_q, not_25_out, not_26_out);
  and and_18 (and_18_out, d_ff_4_q, d_ff_3_q, not_27_out);
  and and_19 (and_19_out, not_28_out, not_29_out, not_30_out);
  and and_20 (and_20_out, not_31_out, d_ff_1_q);
  and and_21 (and_21_out, d_ff_3_q, d_ff_1_q);
  and and_22 (and_22_out, not_32_out, d_ff_3_q, d_ff_2_q);
  and and_23 (and_23_out, d_ff_4_q, not_33_out, not_34_out);
  and and_24 (and_24_out, d_ff_4_q, not_35_out, d_ff_2_q);
  and and_25 (and_25_out, not_36_out, not_37_out, not_38_out);
  and and_26 (and_26_out, d_ff_2_q, d_ff_1_q);
  and and_27 (and_27_out, d_ff_3_q, d_ff_1_q);
  and and_28 (and_28_out, not_39_out, d_ff_3_q, d_ff_2_q);
  and and_29 (and_29_out, not_40_out, not_41_out, not_42_out);
  and and_30 (and_30_out, not_43_out, not_44_out, d_ff_1_q);
  and and_31 (and_31_out, not_45_out, d_ff_3_q, d_ff_2_q, not_46_out);
  and and_32 (and_32_out, d_ff_4_q, not_47_out, d_ff_2_q, not_48_out);
  and and_33 (and_33_out, d_ff_4_q, d_ff_3_q, not_49_out, not_50_out);
  and and_34 (and_34_out, d_ff_4_q, d_ff_3_q, d_ff_2_q, d_ff_1_q);
  or or_1 (A_3, and_1_out, and_2_out, and_3_out, and_4_out, and_5_out, and_6_out, and_7_out);
  or or_2 (B_3, and_8_out, and_9_out, and_10_out, and_11_out);
  or or_3 (C_3, and_12_out, and_13_out, and_14_out);
  or or_4 (D_3, and_15_out, and_16_out, and_17_out, and_18_out);
  or or_5 (E_3, and_19_out, and_20_out, and_21_out, and_22_out, and_23_out, and_24_out);
  or or_6 (F_3, and_25_out, and_26_out, and_27_out, and_28_out);
  or or_7 (G_3, and_29_out, and_30_out, and_31_out, and_32_out, and_33_out, and_34_out);
  _7_Segment_Display u_7_segment_display_2 (.g(G_3), .f(F_3), .a(A_3), .b(B_3), .e(E_3), .d(D_3), .c(C_3));  // open: dp
  not not_51 (not_51_out, d_ff_4_q);
  not not_52 (not_52_out, d_ff_3_q);
  not not_53 (not_53_out, d_ff_1_q);
  not not_54 (not_54_out, d_ff_2_q);
  not not_55 (not_55_out, d_ff_4_q);
  not not_56 (not_56_out, d_ff_3_q);
  not not_57 (not_57_out, d_ff_1_q);
  not not_58 (not_58_out, d_ff_2_q);
  not not_59 (not_59_out, d_ff_3_q);
  not not_60 (not_60_out, d_ff_2_q);
  not not_61 (not_61_out, d_ff_4_q);
  not not_62 (not_62_out, d_ff_2_q);
  not not_63 (not_63_out, d_ff_3_q);
  not not_64 (not_64_out, d_ff_1_q);
  not not_65 (not_65_out, d_ff_2_q);
  not not_66 (not_66_out, d_ff_1_q);
  not not_67 (not_67_out, d_ff_4_q);
  not not_68 (not_68_out, d_ff_3_q);
  not not_69 (not_69_out, d_ff_1_q);
  not not_70 (not_70_out, d_ff_1_q);
  not not_71 (not_71_out, d_ff_4_q);
  not not_72 (not_72_out, d_ff_1_q);
  not not_73 (not_73_out, d_ff_1_q);
  not not_74 (not_74_out, d_ff_1_q);
  not not_75 (not_75_out, d_ff_4_q);
  not not_76 (not_76_out, d_ff_2_q);
  not not_77 (not_77_out, d_ff_1_q);
  not not_78 (not_78_out, d_ff_4_q);
  not not_79 (not_79_out, d_ff_2_q);
  and and_35 (and_35_out, not_51_out, not_52_out, not_53_out);
  and and_36 (and_36_out, d_ff_3_q, not_54_out);
  and and_37 (and_37_out, d_ff_4_q, d_ff_1_q);
  and and_38 (and_38_out, d_ff_4_q, d_ff_2_q);
  and and_39 (and_39_out, not_55_out, not_56_out, not_57_out);
  and and_40 (and_40_out, not_58_out, d_ff_1_q);
  and and_41 (and_41_out, d_ff_4_q, not_59_out, d_ff_2_q);
  and and_42 (and_42_out, d_ff_4_q, d_ff_3_q, not_60_out);
  and and_43 (and_43_out, not_61_out, not_62_out, d_ff_1_q);
  and and_44 (and_44_out, not_63_out, d_ff_2_q, not_64_out);
  and and_45 (and_45_out, d_ff_4_q, d_ff_3_q, not_65_out, not_66_out);
  and and_46 (and_46_out, not_67_out, not_68_out, not_69_out);
  and and_47 (and_47_out, d_ff_2_q, not_70_out);
  and and_48 (and_48_out, d_ff_3_q, d_ff_2_q);
  and and_49 (and_49_out, d_ff_4_q, d_ff_1_q);
  and and_50 (and_50_out, d_ff_4_q, d_ff_3_q);
  and and_51 (and_51_out, not_71_out, not_72_out);
  and and_52 (and_52_out, d_ff_2_q, not_73_out);
  and and_53 (and_53_out, d_ff_4_q, d_ff_1_q);
  and and_54 (and_54_out, d_ff_2_q, not_74_out);
  or or_8 (F, and_54_out, d_ff_3_q);
  and and_55 (and_55_out, not_75_out, not_76_out, not_77_out);
  and and_56 (and_56_out, not_78_out, d_ff_3_q, not_79_out);
  and and_57 (and_57_out, d_ff_4_q, d_ff_1_q);
  and and_58 (and_58_out, d_ff_4_q, d_ff_3_q, d_ff_2_q);
  or or_9 (A, and_35_out, and_36_out, and_37_out, and_38_out);
  or or_10 (B, and_39_out, and_40_out, and_41_out, and_42_out);
  or or_11 (C, and_43_out, and_44_out, and_45_out);
  or or_12 (D, and_46_out, and_47_out, and_48_out, and_49_out, and_50_out);
  or or_13 (E, and_51_out, and_52_out, d_ff_3_q, and_53_out);
  or or_14 (G, and_55_out, and_56_out, and_57_out, and_58_out);
  _7_Segment_Display u_7_segment_display_3 (.g(G), .f(F), .a(A), .b(B), .e(E), .d(D), .c(C));  // open: dp
  not not_80 (not_80_out, d_ff_3_q);
  not not_81 (not_81_out, d_ff_4_q);
  not not_82 (not_82_out, d_ff_2_q);
  not not_83 (not_83_out, d_ff_1_q);
  not not_84 (not_84_out, d_ff_3_q);
  not not_85 (not_85_out, d_ff_4_q);
  not not_86 (not_86_out, d_ff_2_q);
  not not_87 (not_87_out, d_ff_1_q);
  not not_88 (not_88_out, d_ff_3_q);
  not not_89 (not_89_out, d_ff_2_q);
  not not_90 (not_90_out, d_ff_3_q);
  not not_91 (not_91_out, d_ff_4_q);
  not not_92 (not_92_out, d_ff_3_q);
  not not_93 (not_93_out, d_ff_2_q);
  not not_94 (not_94_out, d_ff_4_q);
  not not_95 (not_95_out, d_ff_2_q);
  not not_96 (not_96_out, d_ff_1_q);
  not not_97 (not_97_out, d_ff_3_q);
  not not_98 (not_98_out, d_ff_2_q);
  not not_99 (not_99_out, d_ff_1_q);
  not not_100 (not_100_out, d_ff_3_q);
  not not_101 (not_101_out, d_ff_3_q);
  not not_102 (not_102_out, d_ff_2_q);
  not not_103 (not_103_out, d_ff_4_q);
  not not_104 (not_104_out, d_ff_1_q);
  not not_105 (not_105_out, d_ff_3_q);
  not not_106 (not_106_out, d_ff_3_q);
  not not_107 (not_107_out, d_ff_2_q);
  not not_108 (not_108_out, d_ff_4_q);
  not not_109 (not_109_out, d_ff_2_q);
  not not_110 (not_110_out, d_ff_1_q);
  not not_111 (not_111_out, d_ff_4_q);
  not not_112 (not_112_out, d_ff_3_q);
  not not_113 (not_113_out, d_ff_4_q);
  not not_114 (not_114_out, d_ff_2_q);
  not not_115 (not_115_out, d_ff_1_q);
  not not_116 (not_116_out, d_ff_3_q);
  not not_117 (not_117_out, d_ff_1_q);
  not not_118 (not_118_out, d_ff_1_q);
  and and_59 (and_59_out, not_80_out, d_ff_1_q);
  and and_60 (and_60_out, not_81_out, d_ff_3_q, not_82_out, not_83_out);
  and and_61 (and_61_out, d_ff_4_q, not_84_out);
  and and_62 (and_62_out, d_ff_4_q, d_ff_1_q);
  and and_63 (and_63_out, d_ff_4_q, d_ff_2_q);
  and and_64 (and_64_out, not_85_out, not_86_out, not_87_out);
  and and_65 (and_65_out, not_88_out, not_89_out);
  and and_66 (and_66_out, d_ff_4_q, not_90_out);
  and and_67 (and_67_out, d_ff_4_q, d_ff_2_q, d_ff_1_q);
  and and_68 (and_68_out, not_91_out, not_92_out, not_93_out);
  and and_69 (and_69_out, not_94_out, not_95_out, not_96_out);
  and and_70 (and_70_out, d_ff_4_q, not_97_out, d_ff_1_q);
  and and_71 (and_71_out, not_98_out, d_ff_1_q);
  and and_72 (and_72_out, d_ff_3_q, d_ff_2_q, not_99_out);
  and and_73 (and_73_out, d_ff_4_q, not_100_out);
  and and_74 (and_74_out, d_ff_4_q, d_ff_1_q);
  and and_75 (and_75_out, not_101_out, d_ff_1_q);
  and and_76 (and_76_out, not_102_out, d_ff_1_q);
  and and_77 (and_77_out, not_103_out, d_ff_3_q, not_104_out);
  and and_78 (and_78_out, d_ff_4_q, not_105_out);
  and and_79 (and_79_out, d_ff_4_q, d_ff_2_q);
  and and_80 (and_80_out, not_106_out, d_ff_1_q);
  and and_81 (and_81_out, not_107_out, d_ff_1_q);
  and and_82 (and_82_out, not_108_out, d_ff_3_q, not_109_out);
  and and_83 (and_83_out, d_ff_3_q, d_ff_2_q, not_110_out);
  and and_84 (and_84_out, not_111_out, not_112_out, d_ff_2_q, d_ff_1_q);
  and and_85 (and_85_out, not_113_out, d_ff_3_q, not_114_out, not_115_out);
  and and_86 (and_86_out, d_ff_4_q, not_116_out, not_117_out);
  and and_87 (and_87_out, d_ff_4_q, d_ff_2_q, not_118_out);
  and and_88 (and_88_out, d_ff_4_q, d_ff_3_q, d_ff_1_q);
  or or_15 (A_2, and_59_out, and_60_out, and_61_out, and_62_out, and_63_out);
  or or_16 (B_2, and_64_out, and_65_out, and_66_out, and_67_out);
  or or_17 (C_2, and_68_out, and_69_out, and_70_out);
  or or_18 (D_2, and_71_out, and_72_out, and_73_out, and_74_out);
  or or_19 (E_2, and_75_out, and_76_out, and_77_out, and_78_out, and_79_out);
  or or_20 (F_2, and_80_out, and_81_out, and_82_out, and_83_out);
  or or_21 (G_2, and_84_out, and_85_out, and_86_out, and_87_out, and_88_out);
  _7_Segment_Display u_7_segment_display_4 (.g(G_2), .f(F_2), .a(A_2), .b(B_2), .e(E_2), .d(D_2), .c(C_2));  // open: dp

  // Notes on the sheet:
  //   D
  //   C
  //   B
  //   A
endmodule

module Display_1 (
  output A,
  output B,
  output C,
  output D,
  output E,
  output F,
  output G
);

  wire clock_1_out, d_ff_1_q, d_ff_1_qn, d_ff_2_q, d_ff_2_qn, d_ff_3_q, d_ff_3_qn, d_ff_4_q, d_ff_4_qn,
       nand_1_out, nand_2_out, nand_3_out, nand_4_out, nand_5_out, nand_6_out, nand_7_out, nand_8_out,
       nand_9_out, nand_10_out, nand_11_out, nand_12_out, nand_13_out, nand_14_out, nand_15_out, nand_16_out,
       nand_17_out, nand_18_out, nand_19_out, nand_20_out, nand_21_out, nand_22_out, nand_23_out,
       nand_24_out, nand_25_out, nand_26_out, nand_27_out, nand_28_out, nand_29_out, nand_30_out,
       nand_31_out, nand_32_out, nand_33_out, nand_34_out, nand_35_out, nand_36_out, nand_37_out,
       nand_38_out, nand_39_out, nand_40_out, nand_41_out, nand_42_out, nand_43_out, nand_44_out,
       nand_45_out, nand_46_out, nand_47_out, nand_48_out, nand_49_out, nand_50_out, nand_51_out,
       nand_52_out, nand_53_out, nand_54_out, nand_55_out, nand_56_out, nand_57_out, nand_58_out,
       nand_59_out, nand_60_out, nand_61_out, nand_62_out, nand_63_out, nand_64_out, nand_65_out,
       nand_66_out, nand_67_out, nand_68_out, nand_69_out, nand_70_out, nand_71_out, nand_72_out,
       nand_73_out, nand_74_out, nand_75_out, nand_76_out, nand_77_out, nand_78_out, nand_79_out,
       nand_80_out, nand_81_out, nand_82_out, nand_83_out, nand_84_out, nand_85_out, nand_86_out, nand_87_out;

  Clock clock_1 (.out(clock_1_out));
  D_Flip_Flop d_ff_1 (.clk(clock_1_out), .D(d_ff_1_qn), .Q(d_ff_1_q), .Qn(d_ff_1_qn));  // open: preset, en, reset
  D_Flip_Flop d_ff_2 (.clk(d_ff_1_qn), .D(d_ff_2_qn), .Q(d_ff_2_q), .Qn(d_ff_2_qn));  // open: preset, en, reset
  D_Flip_Flop d_ff_3 (.clk(d_ff_2_qn), .D(d_ff_3_qn), .Q(d_ff_3_q), .Qn(d_ff_3_qn));  // open: preset, en, reset
  D_Flip_Flop d_ff_4 (.clk(d_ff_3_qn), .D(d_ff_4_qn), .Q(d_ff_4_q), .Qn(d_ff_4_qn));  // open: preset, en, reset
  nand nand_1 (nand_1_out, d_ff_4_q, d_ff_4_q);
  nand nand_2 (nand_2_out, d_ff_3_q, d_ff_3_q);
  nand nand_3 (nand_3_out, d_ff_2_q, d_ff_2_q);
  nand nand_4 (nand_4_out, d_ff_4_q, d_ff_4_q);
  nand nand_5 (nand_5_out, d_ff_1_q, d_ff_1_q);
  nand nand_6 (nand_6_out, d_ff_1_q, d_ff_1_q);
  nand nand_7 (nand_7_out, d_ff_4_q, d_ff_4_q);
  nand nand_8 (nand_8_out, d_ff_3_q, d_ff_3_q);
  nand nand_9 (nand_9_out, d_ff_2_q, d_ff_2_q);
  nand nand_10 (nand_10_out, d_ff_4_q, d_ff_4_q);
  nand nand_11 (nand_11_out, d_ff_3_q, d_ff_3_q);
  nand nand_12 (nand_12_out, d_ff_4_q, d_ff_4_q);
  nand nand_13 (nand_13_out, d_ff_3_q, d_ff_3_q);
  nand nand_14 (nand_14_out, d_ff_2_q, d_ff_2_q);
  nand nand_15 (nand_15_out, d_ff_1_q, d_ff_1_q);
  nand nand_16 (nand_16_out, d_ff_2_q, d_ff_2_q);
  nand nand_17 (nand_17_out, d_ff_1_q, d_ff_1_q);
  nand nand_18 (nand_18_out, d_ff_4_q, d_ff_4_q);
  nand nand_19 (nand_19_out, d_ff_2_q, d_ff_2_q);
  nand nand_20 (nand_20_out, d_ff_1_q, d_ff_1_q);
  nand nand_21 (nand_21_out, d_ff_1_q, d_ff_1_q);
  nand nand_22 (nand_22_out, d_ff_4_q, d_ff_4_q);
  nand nand_23 (nand_23_out, d_ff_3_q, d_ff_3_q);
  nand nand_24 (nand_24_out, d_ff_1_q, d_ff_1_q);
  nand nand_25 (nand_25_out, d_ff_3_q, d_ff_3_q);
  nand nand_26 (nand_26_out, d_ff_2_q, d_ff_2_q);
  nand nand_27 (nand_27_out, d_ff_2_q, d_ff_2_q);
  nand nand_28 (nand_28_out, d_ff_1_q, d_ff_1_q);
  nand nand_29 (nand_29_out, d_ff_2_q, d_ff_2_q);
  nand nand_30 (nand_30_out, d_ff_3_q, d_ff_3_q);
  nand nand_31 (nand_31_out, d_ff_1_q, d_ff_1_q);
  nand nand_32 (nand_32_out, d_ff_4_q, d_ff_4_q);
  nand nand_33 (nand_33_out, d_ff_1_q, d_ff_1_q);
  nand nand_34 (nand_34_out, d_ff_3_q, d_ff_3_q);
  nand nand_35 (nand_35_out, d_ff_2_q, d_ff_2_q);
  nand nand_36 (nand_36_out, d_ff_1_q, d_ff_1_q);
  nand nand_37 (nand_37_out, d_ff_4_q, d_ff_4_q);
  nand nand_38 (nand_38_out, d_ff_2_q, d_ff_2_q);
  nand nand_39 (nand_39_out, d_ff_3_q, d_ff_3_q);
  nand nand_40 (nand_40_out, d_ff_3_q, d_ff_3_q);
  nand nand_41 (nand_41_out, d_ff_2_q, d_ff_2_q);
  nand nand_42 (nand_42_out, d_ff_1_q, d_ff_1_q);
  nand nand_43 (nand_43_out, d_ff_4_q, d_ff_4_q);
  nand nand_44 (nand_44_out, d_ff_4_q, d_ff_4_q);
  nand nand_45 (nand_45_out, d_ff_3_q, d_ff_3_q);
  nand nand_46 (nand_46_out, d_ff_2_q, d_ff_2_q);
  nand nand_47 (nand_47_out, d_ff_4_q, d_ff_4_q);
  nand nand_48 (nand_48_out, d_ff_3_q, d_ff_3_q);
  nand nand_49 (nand_49_out, d_ff_1_q, d_ff_1_q);
  nand nand_50 (nand_50_out, d_ff_4_q, d_ff_4_q);
  nand nand_51 (nand_51_out, d_ff_3_q, d_ff_3_q);
  nand nand_52 (nand_52_out, d_ff_2_q, d_ff_2_q);
  nand nand_53 (nand_53_out, nand_1_out, nand_2_out, nand_3_out);
  nand nand_54 (nand_54_out, nand_4_out, nand_5_out);
  nand nand_55 (nand_55_out, d_ff_3_q, nand_6_out);
  nand nand_56 (nand_56_out, nand_7_out, d_ff_3_q, d_ff_2_q);
  nand nand_57 (nand_57_out, d_ff_4_q, nand_8_out, d_ff_2_q, d_ff_1_q);
  nand nand_58 (nand_58_out, d_ff_4_q, d_ff_3_q, nand_9_out);
  nand nand_59 (nand_59_out, nand_10_out, nand_11_out, d_ff_2_q);
  nand nand_60 (nand_60_out, nand_12_out, d_ff_2_q, d_ff_1_q);
  nand nand_61 (nand_61_out, nand_13_out, d_ff_2_q, d_ff_1_q);
  nand nand_62 (nand_62_out, d_ff_3_q, nand_14_out, nand_15_out);
  nand nand_63 (nand_63_out, d_ff_4_q, d_ff_3_q, nand_16_out);
  nand nand_64 (nand_64_out, d_ff_4_q, d_ff_3_q, nand_17_out);
  nand nand_65 (nand_65_out, nand_18_out, d_ff_2_q, d_ff_1_q);
  nand nand_66 (nand_66_out, d_ff_3_q, nand_19_out, nand_20_out);
  nand nand_67 (nand_67_out, d_ff_4_q, d_ff_3_q, nand_21_out);
  nand nand_68 (nand_68_out, nand_22_out, nand_23_out, nand_24_out);
  nand nand_69 (nand_69_out, nand_25_out, nand_26_out);
  nand nand_70 (nand_70_out, nand_27_out, nand_28_out);
  nand nand_71 (nand_71_out, d_ff_4_q, nand_29_out);
  nand nand_72 (nand_72_out, d_ff_4_q, nand_30_out, d_ff_1_q);
  nand nand_73 (nand_73_out, d_ff_4_q, d_ff_3_q, nand_31_out);
  nand nand_74 (nand_74_out, nand_32_out, nand_33_out);
  nand nand_75 (nand_75_out, nand_34_out, nand_35_out);
  nand nand_76 (nand_76_out, d_ff_3_q, nand_36_out);
  nand nand_77 (nand_77_out, nand_37_out, d_ff_3_q, d_ff_2_q);
  nand nand_78 (nand_78_out, d_ff_4_q, nand_38_out);
  nand nand_79 (nand_79_out, d_ff_4_q, nand_39_out, d_ff_1_q);
  nand nand_80 (nand_80_out, nand_40_out, nand_41_out);
  nand nand_81 (nand_81_out, d_ff_3_q, nand_42_out);
  nand nand_82 (nand_82_out, nand_43_out, d_ff_3_q, d_ff_2_q);
  nand nand_83 (nand_83_out, nand_44_out, nand_45_out, nand_46_out);
  nand nand_84 (nand_84_out, nand_47_out, nand_48_out, nand_49_out);
  nand nand_85 (nand_85_out, nand_50_out, d_ff_3_q, d_ff_2_q);
  nand nand_86 (nand_86_out, d_ff_4_q, nand_51_out, d_ff_2_q, d_ff_1_q);
  nand nand_87 (nand_87_out, d_ff_4_q, d_ff_3_q, nand_52_out, d_ff_1_q);
  nand nand_88 (A, nand_53_out, nand_54_out, nand_55_out, nand_56_out, nand_57_out, nand_58_out);
  nand nand_89 (B, nand_59_out, nand_60_out, nand_61_out, nand_62_out, nand_63_out, nand_64_out);
  nand nand_90 (C, nand_65_out, nand_66_out, nand_67_out);
  nand nand_91 (D, nand_68_out, nand_69_out, nand_70_out, nand_71_out, nand_72_out, nand_73_out);
  nand nand_92 (E, nand_74_out, nand_75_out, nand_76_out, nand_77_out, nand_78_out, nand_79_out);
  nand nand_93 (F, nand_80_out, nand_81_out, nand_82_out);
  nand nand_94 (G, nand_83_out, nand_84_out, nand_85_out, nand_86_out, nand_87_out);
  _7_Segment_Display u_7_segment_display_1 (.g(G), .f(F), .a(A), .b(B), .e(E), .d(D), .c(C));  // open: dp

  // Notes on the sheet:
  //   D
  //   C
  //   B
  //   A
endmodule

module Display_2 (
  output A,
  output B,
  output C,
  output D,
  output E,
  output F,
  output G
);

  wire and_1_out, and_2_out, and_3_out, and_4_out, and_5_out, and_6_out, and_7_out, and_8_out, and_9_out,
       and_10_out, and_11_out, and_12_out, and_13_out, and_14_out, and_15_out, and_16_out, and_17_out,
       and_18_out, and_19_out, and_20_out, and_21_out, and_22_out, and_23_out, and_24_out, and_25_out,
       and_26_out, and_27_out, and_28_out, and_29_out, and_30_out, and_31_out, and_32_out, and_33_out,
       and_34_out, clock_1_out, d_ff_1_q, d_ff_1_qn, d_ff_2_q, d_ff_2_qn, d_ff_3_q, d_ff_3_qn, d_ff_4_q,
       d_ff_4_qn, not_1_out, not_2_out, not_3_out, not_4_out, not_5_out, not_6_out, not_7_out, not_8_out,
       not_9_out, not_10_out, not_11_out, not_12_out, not_13_out, not_14_out, not_15_out, not_16_out,
       not_17_out, not_18_out, not_19_out, not_20_out, not_21_out, not_22_out, not_23_out, not_24_out,
       not_25_out, not_26_out, not_27_out, not_28_out, not_29_out, not_30_out, not_31_out, not_32_out,
       not_33_out, not_34_out, not_35_out, not_36_out, not_37_out, not_38_out, not_39_out, not_40_out,
       not_41_out, not_42_out, not_43_out, not_44_out, not_45_out, not_46_out, not_47_out, not_48_out,
       not_49_out, not_50_out;

  Clock clock_1 (.out(clock_1_out));
  D_Flip_Flop d_ff_1 (.clk(clock_1_out), .D(d_ff_1_qn), .Q(d_ff_1_q), .Qn(d_ff_1_qn));  // open: preset, en, reset
  D_Flip_Flop d_ff_2 (.clk(d_ff_1_qn), .D(d_ff_2_qn), .Q(d_ff_2_q), .Qn(d_ff_2_qn));  // open: preset, en, reset
  D_Flip_Flop d_ff_3 (.clk(d_ff_2_qn), .D(d_ff_3_qn), .Q(d_ff_3_q), .Qn(d_ff_3_qn));  // open: preset, en, reset
  D_Flip_Flop d_ff_4 (.clk(d_ff_3_qn), .D(d_ff_4_qn), .Q(d_ff_4_q), .Qn(d_ff_4_qn));  // open: preset, en, reset
  not not_1 (not_1_out, d_ff_4_q);
  not not_2 (not_2_out, d_ff_3_q);
  not not_3 (not_3_out, d_ff_2_q);
  not not_4 (not_4_out, d_ff_4_q);
  not not_5 (not_5_out, d_ff_3_q);
  not not_6 (not_6_out, d_ff_4_q);
  not not_7 (not_7_out, d_ff_2_q);
  not not_8 (not_8_out, d_ff_4_q);
  not not_9 (not_9_out, d_ff_1_q);
  not not_10 (not_10_out, d_ff_3_q);
  not not_11 (not_11_out, d_ff_2_q);
  not not_12 (not_12_out, d_ff_4_q);
  not not_13 (not_13_out, d_ff_3_q);
  not not_14 (not_14_out, d_ff_4_q);
  not not_15 (not_15_out, d_ff_1_q);
  not not_16 (not_16_out, d_ff_3_q);
  not not_17 (not_17_out, d_ff_2_q);
  not not_18 (not_18_out, d_ff_4_q);
  not not_19 (not_19_out, d_ff_1_q);
  not not_20 (not_20_out, d_ff_3_q);
  not not_21 (not_21_out, d_ff_2_q);
  not not_22 (not_22_out, d_ff_4_q);
  not not_23 (not_23_out, d_ff_3_q);
  not not_24 (not_24_out, d_ff_2_q);
  not not_25 (not_25_out, d_ff_3_q);
  not not_26 (not_26_out, d_ff_1_q);
  not not_27 (not_27_out, d_ff_2_q);
  not not_28 (not_28_out, d_ff_3_q);
  not not_29 (not_29_out, d_ff_2_q);
  not not_30 (not_30_out, d_ff_1_q);
  not not_31 (not_31_out, d_ff_4_q);
  not not_32 (not_32_out, d_ff_4_q);
  not not_33 (not_33_out, d_ff_2_q);
  not not_34 (not_34_out, d_ff_1_q);
  not not_35 (not_35_out, d_ff_3_q);
  not not_36 (not_36_out, d_ff_3_q);
  not not_37 (not_37_out, d_ff_2_q);
  not not_38 (not_38_out, d_ff_1_q);
  not not_39 (not_39_out, d_ff_4_q);
  not not_40 (not_40_out, d_ff_4_q);
  not not_41 (not_41_out, d_ff_3_q);
  not not_42 (not_42_out, d_ff_2_q);
  not not_43 (not_43_out, d_ff_4_q);
  not not_44 (not_44_out, d_ff_2_q);
  not not_45 (not_45_out, d_ff_4_q);
  not not_46 (not_46_out, d_ff_1_q);
  not not_47 (not_47_out, d_ff_3_q);
  not not_48 (not_48_out, d_ff_1_q);
  not not_49 (not_49_out, d_ff_2_q);
  not not_50 (not_50_out, d_ff_1_q);
  and and_1 (and_1_out, not_1_out, not_2_out, not_3_out);
  and and_2 (and_2_out, not_4_out, not_5_out, d_ff_1_q);
  and and_3 (and_3_out, not_6_out, not_7_out, d_ff_1_q);
  and and_4 (and_4_out, not_8_out, d_ff_3_q, d_ff_2_q, not_9_out);
  and and_5 (and_5_out, d_ff_4_q, not_10_out, d_ff_2_q);
  and and_6 (and_6_out, d_ff_4_q, d_ff_3_q, not_11_out);
  and and_7 (and_7_out, d_ff_4_q, d_ff_3_q, d_ff_1_q);
  and and_8 (and_8_out, not_12_out, not_13_out, d_ff_1_q);
  and and_9 (and_9_out, not_14_out, d_ff_2_q, not_15_out);
  and and_10 (and_10_out, not_16_out, d_ff_2_q);
  and and_11 (and_11_out, d_ff_4_q, d_ff_3_q, not_17_out);
  and and_12 (and_12_out, not_18_out, d_ff_2_q, not_19_out);
  and and_13 (and_13_out, not_20_out, d_ff_2_q, d_ff_1_q);
  and and_14 (and_14_out, d_ff_4_q, d_ff_3_q, not_21_out, d_ff_1_q);
  and and_15 (and_15_out, not_22_out, not_23_out, not_24_out);
  and and_16 (and_16_out, d_ff_2_q, d_ff_1_q);
  and and_17 (and_17_out, d_ff_4_q, not_25_out, not_26_out);
  and and_18 (and_18_out, d_ff_4_q, d_ff_3_q, not_27_out);
  and and_19 (and_19_out, not_28_out, not_29_out, not_30_out);
  and and_20 (and_20_out, not_31_out, d_ff_1_q);
  and and_21 (and_21_out, d_ff_3_q, d_ff_1_q);
  and and_22 (and_22_out, not_32_out, d_ff_3_q, d_ff_2_q);
  and and_23 (and_23_out, d_ff_4_q, not_33_out, not_34_out);
  and and_24 (and_24_out, d_ff_4_q, not_35_out, d_ff_2_q);
  and and_25 (and_25_out, not_36_out, not_37_out, not_38_out);
  and and_26 (and_26_out, d_ff_2_q, d_ff_1_q);
  and and_27 (and_27_out, d_ff_3_q, d_ff_1_q);
  and and_28 (and_28_out, not_39_out, d_ff_3_q, d_ff_2_q);
  and and_29 (and_29_out, not_40_out, not_41_out, not_42_out);
  and and_30 (and_30_out, not_43_out, not_44_out, d_ff_1_q);
  and and_31 (and_31_out, not_45_out, d_ff_3_q, d_ff_2_q, not_46_out);
  and and_32 (and_32_out, d_ff_4_q, not_47_out, d_ff_2_q, not_48_out);
  and and_33 (and_33_out, d_ff_4_q, d_ff_3_q, not_49_out, not_50_out);
  and and_34 (and_34_out, d_ff_4_q, d_ff_3_q, d_ff_2_q, d_ff_1_q);
  or or_1 (A, and_1_out, and_2_out, and_3_out, and_4_out, and_5_out, and_6_out, and_7_out);
  or or_2 (B, and_8_out, and_9_out, and_10_out, and_11_out);
  or or_3 (C, and_12_out, and_13_out, and_14_out);
  or or_4 (D, and_15_out, and_16_out, and_17_out, and_18_out);
  or or_5 (E, and_19_out, and_20_out, and_21_out, and_22_out, and_23_out, and_24_out);
  or or_6 (F, and_25_out, and_26_out, and_27_out, and_28_out);
  or or_7 (G, and_29_out, and_30_out, and_31_out, and_32_out, and_33_out, and_34_out);
  _7_Segment_Display u_7_segment_display_1 (.g(G), .f(F), .a(A), .b(B), .e(E), .d(D), .c(C));  // open: dp

  // Notes on the sheet:
  //   D
  //   C
  //   B
  //   A
endmodule

module Display_3 (
  output A,
  output B,
  output C,
  output D,
  output E,
  output F,
  output G
);

  wire and_1_out, and_2_out, and_3_out, and_4_out, and_5_out, and_6_out, and_7_out, and_8_out, and_9_out,
       and_10_out, and_11_out, and_12_out, and_13_out, and_14_out, and_15_out, and_16_out, and_17_out,
       and_18_out, and_19_out, and_20_out, and_21_out, and_22_out, and_23_out, and_24_out, clock_1_out,
       d_ff_1_q, d_ff_1_qn, d_ff_2_q, d_ff_2_qn, d_ff_3_q, d_ff_3_qn, d_ff_4_q, d_ff_4_qn, not_1_out,
       not_2_out, not_3_out, not_4_out, not_5_out, not_6_out, not_7_out, not_8_out, not_9_out, not_10_out,
       not_11_out, not_12_out, not_13_out, not_14_out, not_15_out, not_16_out, not_17_out, not_18_out,
       not_19_out, not_20_out, not_21_out, not_22_out, not_23_out, not_24_out, not_25_out, not_26_out,
       not_27_out, not_28_out, not_29_out;

  Clock clock_1 (.out(clock_1_out));
  D_Flip_Flop d_ff_1 (.clk(clock_1_out), .D(d_ff_1_qn), .Q(d_ff_1_q), .Qn(d_ff_1_qn));  // open: preset, en, reset
  D_Flip_Flop d_ff_2 (.clk(d_ff_1_qn), .D(d_ff_2_qn), .Q(d_ff_2_q), .Qn(d_ff_2_qn));  // open: preset, en, reset
  D_Flip_Flop d_ff_3 (.clk(d_ff_2_qn), .D(d_ff_3_qn), .Q(d_ff_3_q), .Qn(d_ff_3_qn));  // open: preset, en, reset
  D_Flip_Flop d_ff_4 (.clk(d_ff_3_qn), .D(d_ff_4_qn), .Q(d_ff_4_q), .Qn(d_ff_4_qn));  // open: preset, en, reset
  not not_1 (not_1_out, d_ff_4_q);
  not not_2 (not_2_out, d_ff_3_q);
  not not_3 (not_3_out, d_ff_1_q);
  not not_4 (not_4_out, d_ff_2_q);
  not not_5 (not_5_out, d_ff_4_q);
  not not_6 (not_6_out, d_ff_3_q);
  not not_7 (not_7_out, d_ff_1_q);
  not not_8 (not_8_out, d_ff_2_q);
  not not_9 (not_9_out, d_ff_3_q);
  not not_10 (not_10_out, d_ff_2_q);
  not not_11 (not_11_out, d_ff_4_q);
  not not_12 (not_12_out, d_ff_2_q);
  not not_13 (not_13_out, d_ff_3_q);
  not not_14 (not_14_out, d_ff_1_q);
  not not_15 (not_15_out, d_ff_2_q);
  not not_16 (not_16_out, d_ff_1_q);
  not not_17 (not_17_out, d_ff_4_q);
  not not_18 (not_18_out, d_ff_3_q);
  not not_19 (not_19_out, d_ff_1_q);
  not not_20 (not_20_out, d_ff_1_q);
  not not_21 (not_21_out, d_ff_4_q);
  not not_22 (not_22_out, d_ff_1_q);
  not not_23 (not_23_out, d_ff_1_q);
  not not_24 (not_24_out, d_ff_1_q);
  not not_25 (not_25_out, d_ff_4_q);
  not not_26 (not_26_out, d_ff_2_q);
  not not_27 (not_27_out, d_ff_1_q);
  not not_28 (not_28_out, d_ff_4_q);
  not not_29 (not_29_out, d_ff_2_q);
  and and_1 (and_1_out, not_1_out, not_2_out, not_3_out);
  and and_2 (and_2_out, d_ff_3_q, not_4_out);
  and and_3 (and_3_out, d_ff_4_q, d_ff_1_q);
  and and_4 (and_4_out, d_ff_4_q, d_ff_2_q);
  and and_5 (and_5_out, not_5_out, not_6_out, not_7_out);
  and and_6 (and_6_out, not_8_out, d_ff_1_q);
  and and_7 (and_7_out, d_ff_4_q, not_9_out, d_ff_2_q);
  and and_8 (and_8_out, d_ff_4_q, d_ff_3_q, not_10_out);
  and and_9 (and_9_out, not_11_out, not_12_out, d_ff_1_q);
  and and_10 (and_10_out, not_13_out, d_ff_2_q, not_14_out);
  and and_11 (and_11_out, d_ff_4_q, d_ff_3_q, not_15_out, not_16_out);
  and and_12 (and_12_out, not_17_out, not_18_out, not_19_out);
  and and_13 (and_13_out, d_ff_2_q, not_20_out);
  and and_14 (and_14_out, d_ff_3_q, d_ff_2_q);
  and and_15 (and_15_out, d_ff_4_q, d_ff_1_q);
  and and_16 (and_16_out, d_ff_4_q, d_ff_3_q);
  and and_17 (and_17_out, not_21_out, not_22_out);
  and and_18 (and_18_out, d_ff_2_q, not_23_out);
  and and_19 (and_19_out, d_ff_4_q, d_ff_1_q);
  and and_20 (and_20_out, d_ff_2_q, not_24_out);
  and and_21 (and_21_out, not_25_out, not_26_out, not_27_out);
  and and_22 (and_22_out, not_28_out, d_ff_3_q, not_29_out);
  and and_23 (and_23_out, d_ff_4_q, d_ff_1_q);
  and and_24 (and_24_out, d_ff_4_q, d_ff_3_q, d_ff_2_q);
  or or_1 (A, and_1_out, and_2_out, and_3_out, and_4_out);
  or or_2 (B, and_5_out, and_6_out, and_7_out, and_8_out);
  or or_3 (C, and_9_out, and_10_out, and_11_out);
  or or_4 (D, and_12_out, and_13_out, and_14_out, and_15_out, and_16_out);
  or or_5 (E, and_17_out, and_18_out, d_ff_3_q, and_19_out);
  or or_6 (F, and_20_out, d_ff_3_q);
  or or_7 (G, and_21_out, and_22_out, and_23_out, and_24_out);
  _7_Segment_Display u_7_segment_display_1 (.g(G), .f(F), .a(A), .b(B), .e(E), .d(D), .c(C));  // open: dp

  // Notes on the sheet:
  //   D
  //   C
  //   B
  //   A
endmodule

module Display_4 (
  output A,
  output B,
  output C,
  output D,
  output E,
  output F,
  output G
);

  wire and_1_out, and_2_out, and_3_out, and_4_out, and_5_out, and_6_out, and_7_out, and_8_out, and_9_out,
       and_10_out, and_11_out, and_12_out, and_13_out, and_14_out, and_15_out, and_16_out, and_17_out,
       and_18_out, and_19_out, and_20_out, and_21_out, and_22_out, and_23_out, and_24_out, and_25_out,
       and_26_out, and_27_out, and_28_out, and_29_out, and_30_out, clock_1_out, d_ff_1_q, d_ff_1_qn,
       d_ff_2_q, d_ff_2_qn, d_ff_3_q, d_ff_3_qn, d_ff_4_q, d_ff_4_qn, not_1_out, not_2_out, not_3_out,
       not_4_out, not_5_out, not_6_out, not_7_out, not_8_out, not_9_out, not_10_out, not_11_out, not_12_out,
       not_13_out, not_14_out, not_15_out, not_16_out, not_17_out, not_18_out, not_19_out, not_20_out,
       not_21_out, not_22_out, not_23_out, not_24_out, not_25_out, not_26_out, not_27_out, not_28_out,
       not_29_out, not_30_out, not_31_out, not_32_out, not_33_out, not_34_out, not_35_out, not_36_out,
       not_37_out, not_38_out, not_39_out;

  Clock clock_1 (.out(clock_1_out));
  D_Flip_Flop d_ff_1 (.clk(clock_1_out), .D(d_ff_1_qn), .Q(d_ff_1_q), .Qn(d_ff_1_qn));  // open: preset, en, reset
  D_Flip_Flop d_ff_2 (.clk(d_ff_1_qn), .D(d_ff_2_qn), .Q(d_ff_2_q), .Qn(d_ff_2_qn));  // open: preset, en, reset
  D_Flip_Flop d_ff_3 (.clk(d_ff_2_qn), .D(d_ff_3_qn), .Q(d_ff_3_q), .Qn(d_ff_3_qn));  // open: preset, en, reset
  D_Flip_Flop d_ff_4 (.clk(d_ff_3_qn), .D(d_ff_4_qn), .Q(d_ff_4_q), .Qn(d_ff_4_qn));  // open: preset, en, reset
  not not_1 (not_1_out, d_ff_3_q);
  not not_2 (not_2_out, d_ff_4_q);
  not not_3 (not_3_out, d_ff_2_q);
  not not_4 (not_4_out, d_ff_1_q);
  not not_5 (not_5_out, d_ff_3_q);
  not not_6 (not_6_out, d_ff_4_q);
  not not_7 (not_7_out, d_ff_2_q);
  not not_8 (not_8_out, d_ff_1_q);
  not not_9 (not_9_out, d_ff_3_q);
  not not_10 (not_10_out, d_ff_2_q);
  not not_11 (not_11_out, d_ff_3_q);
  not not_12 (not_12_out, d_ff_4_q);
  not not_13 (not_13_out, d_ff_3_q);
  not not_14 (not_14_out, d_ff_2_q);
  not not_15 (not_15_out, d_ff_4_q);
  not not_16 (not_16_out, d_ff_2_q);
  not not_17 (not_17_out, d_ff_1_q);
  not not_18 (not_18_out, d_ff_3_q);
  not not_19 (not_19_out, d_ff_2_q);
  not not_20 (not_20_out, d_ff_1_q);
  not not_21 (not_21_out, d_ff_3_q);
  not not_22 (not_22_out, d_ff_3_q);
  not not_23 (not_23_out, d_ff_2_q);
  not not_24 (not_24_out, d_ff_4_q);
  not not_25 (not_25_out, d_ff_1_q);
  not not_26 (not_26_out, d_ff_3_q);
  not not_27 (not_27_out, d_ff_3_q);
  not not_28 (not_28_out, d_ff_2_q);
  not not_29 (not_29_out, d_ff_4_q);
  not not_30 (not_30_out, d_ff_2_q);
  not not_31 (not_31_out, d_ff_1_q);
  not not_32 (not_32_out, d_ff_4_q);
  not not_33 (not_33_out, d_ff_3_q);
  not not_34 (not_34_out, d_ff_4_q);
  not not_35 (not_35_out, d_ff_2_q);
  not not_36 (not_36_out, d_ff_1_q);
  not not_37 (not_37_out, d_ff_3_q);
  not not_38 (not_38_out, d_ff_1_q);
  not not_39 (not_39_out, d_ff_1_q);
  and and_1 (and_1_out, not_1_out, d_ff_1_q);
  and and_2 (and_2_out, not_2_out, d_ff_3_q, not_3_out, not_4_out);
  and and_3 (and_3_out, d_ff_4_q, not_5_out);
  and and_4 (and_4_out, d_ff_4_q, d_ff_1_q);
  and and_5 (and_5_out, d_ff_4_q, d_ff_2_q);
  and and_6 (and_6_out, not_6_out, not_7_out, not_8_out);
  and and_7 (and_7_out, not_9_out, not_10_out);
  and and_8 (and_8_out, d_ff_4_q, not_11_out);
  and and_9 (and_9_out, d_ff_4_q, d_ff_2_q, d_ff_1_q);
  and and_10 (and_10_out, not_12_out, not_13_out, not_14_out);
  and and_11 (and_11_out, not_15_out, not_16_out, not_17_out);
  and and_12 (and_12_out, d_ff_4_q, not_18_out, d_ff_1_q);
  and and_13 (and_13_out, not_19_out, d_ff_1_q);
  and and_14 (and_14_out, d_ff_3_q, d_ff_2_q, not_20_out);
  and and_15 (and_15_out, d_ff_4_q, not_21_out);
  and and_16 (and_16_out, d_ff_4_q, d_ff_1_q);
  and and_17 (and_17_out, not_22_out, d_ff_1_q);
  and and_18 (and_18_out, not_23_out, d_ff_1_q);
  and and_19 (and_19_out, not_24_out, d_ff_3_q, not_25_out);
  and and_20 (and_20_out, d_ff_4_q, not_26_out);
  and and_21 (and_21_out, d_ff_4_q, d_ff_2_q);
  and and_22 (and_22_out, not_27_out, d_ff_1_q);
  and and_23 (and_23_out, not_28_out, d_ff_1_q);
  and and_24 (and_24_out, not_29_out, d_ff_3_q, not_30_out);
  and and_25 (and_25_out, d_ff_3_q, d_ff_2_q, not_31_out);
  and and_26 (and_26_out, not_32_out, not_33_out, d_ff_2_q, d_ff_1_q);
  and and_27 (and_27_out, not_34_out, d_ff_3_q, not_35_out, not_36_out);
  and and_28 (and_28_out, d_ff_4_q, not_37_out, not_38_out);
  and and_29 (and_29_out, d_ff_4_q, d_ff_2_q, not_39_out);
  and and_30 (and_30_out, d_ff_4_q, d_ff_3_q, d_ff_1_q);
  or or_1 (A, and_1_out, and_2_out, and_3_out, and_4_out, and_5_out);
  or or_2 (B, and_6_out, and_7_out, and_8_out, and_9_out);
  or or_3 (C, and_10_out, and_11_out, and_12_out);
  or or_4 (D, and_13_out, and_14_out, and_15_out, and_16_out);
  or or_5 (E, and_17_out, and_18_out, and_19_out, and_20_out, and_21_out);
  or or_6 (F, and_22_out, and_23_out, and_24_out, and_25_out);
  or or_7 (G, and_26_out, and_27_out, and_28_out, and_29_out, and_30_out);
  _7_Segment_Display u_7_segment_display_1 (.g(G), .f(F), .a(A), .b(B), .e(E), .d(D), .c(C));  // open: dp

  // Notes on the sheet:
  //   D
  //   C
  //   B
  //   A
endmodule

module Counter (
);

  wire clock_1_out, clock_2_out, d_ff_1_q, d_ff_1_qn, d_ff_2_q, d_ff_2_qn, d_ff_3_q, d_ff_3_qn, d_ff_4_q,
       d_ff_4_qn, d_ff_5_q, d_ff_5_qn, d_ff_6_q, d_ff_6_qn, d_ff_7_q, d_ff_7_qn, d_ff_8_q, d_ff_8_qn;

  Clock clock_1 (.out(clock_1_out));
  Clock clock_2 (.out(clock_2_out));
  D_Flip_Flop d_ff_1 (.clk(clock_2_out), .D(d_ff_1_qn), .Q(d_ff_1_q), .Qn(d_ff_1_qn));  // open: preset, en, reset
  D_Flip_Flop d_ff_2 (.clk(d_ff_1_qn), .D(d_ff_2_qn), .Q(d_ff_2_q), .Qn(d_ff_2_qn));  // open: preset, en, reset
  D_Flip_Flop d_ff_3 (.clk(d_ff_2_qn), .D(d_ff_3_qn), .Q(d_ff_3_q), .Qn(d_ff_3_qn));  // open: preset, en, reset
  D_Flip_Flop d_ff_4 (.clk(d_ff_3_qn), .D(d_ff_4_qn), .Q(d_ff_4_q), .Qn(d_ff_4_qn));  // open: preset, en, reset
  D_Flip_Flop d_ff_5 (.clk(clock_1_out), .D(d_ff_5_qn), .Q(d_ff_5_q), .Qn(d_ff_5_qn));  // open: preset, en, reset
  D_Flip_Flop d_ff_6 (.clk(d_ff_5_qn), .D(d_ff_6_qn), .Q(d_ff_6_q), .Qn(d_ff_6_qn));  // open: preset, en, reset
  D_Flip_Flop d_ff_7 (.clk(d_ff_6_qn), .D(d_ff_7_qn), .Q(d_ff_7_q), .Qn(d_ff_7_qn));  // open: preset, en, reset
  D_Flip_Flop d_ff_8 (.clk(d_ff_7_qn), .D(d_ff_8_qn), .Q(d_ff_8_q), .Qn(d_ff_8_qn));  // open: preset, en, reset

  // Notes on the sheet:
  //   D
  //   D
  //   C
  //   B
  //   A
  //   C
  //   B
endmodule
