// Logisim project HW#8.circ as structural Verilog: 3 circuits, main circuit main
module main (
  output A,
  output A_2,
  output B,
  output C,
  output B_2,
  output C_2,
  output D,
  output D_2,
  output E,
  output F,
  output E_2,
  output F_2,
  output G,
  output G_2
);

  wire and_1_out, and_2_out, and_3_out, and_4_out, and_5_out, and_6_out, and_7_out, and_8_out, and_9_out,
       and_10_out, and_11_out, and_12_out, and_13_out, and_14_out, and_15_out, and_16_out, and_17_out,
       and_18_out, and_19_out, and_20_out, and_21_out, and_22_out, and_23_out, and_24_out, and_25_out,
       and_26_out, and_27_out, and_28_out, and_29_out, and_30_out, and_31_out, and_32_out, clock_1_out,
       d_ff_1_q, d_ff_1_qn, d_ff_2_q, d_ff_2_qn, d_ff_3_q, d_ff_3_qn, d_ff_4_q, d_ff_4_qn, d_ff_5_q,
       d_ff_5_qn, d_ff_6_q, d_ff_6_qn, nand_1_out, not_1_out, not_2_out, not_3_out, not_4_out, not_5_out,
       not_6_out, not_7_out, not_8_out, not_9_out, not_10_out, not_11_out, not_12_out, not_13_out,
       not_14_out, not_15_out, not_16_out, not_17_out, not_18_out, not_19_out, not_20_out, not_21_out,
       not_22_out, not_23_out, not_24_out, not_25_out, not_26_out, not_27_out, not_28_out, not_29_out,
       not_30_out, not_31_out, not_32_out, not_33_out, not_34_out;

  D_Flip_Flop d_ff_1 (.clk(nand_1_out), .D(d_ff_1_qn), .Q(d_ff_1_q), .Qn(d_ff_1_qn));  // open: preset, en, reset
  D_Flip_Flop d_ff_2 (.clk(d_ff_1_qn), .D(d_ff_2_qn), .Q(d_ff_2_q), .Qn(d_ff_2_qn));  // open: preset, en, reset
  D_Flip_Flop d_ff_3 (.clk(d_ff_2_qn), .D(d_ff_3_qn), .Q(d_ff_3_q), .Qn(d_ff_3_qn));  // open: preset, en, reset
  nand nand_1 (nand_1_out, d_ff_6_q, d_ff_5_q, d_ff_4_q);
  not not_1 (not_1_out, d_ff_3_q);
  not not_2 (not_2_out, d_ff_1_q);
  not not_3 (not_3_out, d_ff_2_q);
  not not_4 (not_4_out, d_ff_1_q);
  not not_5 (not_5_out, d_ff_3_q);
  not not_6 (not_6_out, d_ff_1_q);
  not not_7 (not_7_out, d_ff_2_q);
  not not_8 (not_8_out, d_ff_3_q);
  not not_9 (not_9_out, d_ff_1_q);
  not not_10 (not_10_out, d_ff_2_q);
  not not_11 (not_11_out, d_ff_2_q);
  not not_12 (not_12_out, d_ff_3_q);
  not not_13 (not_13_out, d_ff_3_q);
  not not_14 (not_14_out, d_ff_3_q);
  not not_15 (not_15_out, d_ff_3_q);
  not not_16 (not_16_out, d_ff_2_q);
  and and_1 (and_1_out, not_1_out, not_2_out);
  not not_17 (not_17_out, d_ff_2_q);
  and and_2 (and_2_out, d_ff_3_q, d_ff_1_q);
  and and_3 (and_3_out, not_3_out, not_4_out);
  and and_4 (and_4_out, d_ff_2_q, d_ff_1_q);
  or or_1 (C_2, not_5_out, not_6_out, d_ff_2_q);
  and and_5 (and_5_out, not_7_out, d_ff_1_q);
  and and_6 (and_6_out, not_8_out, d_ff_2_q, not_9_out);
  and and_7 (and_7_out, d_ff_3_q, not_10_out);
  and and_8 (and_8_out, d_ff_3_q, d_ff_1_q);
  and and_9 (and_9_out, not_11_out, d_ff_1_q);
  and and_10 (and_10_out, d_ff_3_q, d_ff_1_q);
  and and_11 (and_11_out, not_12_out, d_ff_1_q);
  and and_12 (and_12_out, not_13_out, d_ff_2_q);
  and and_13 (and_13_out, d_ff_2_q, d_ff_1_q);
  and and_14 (and_14_out, not_14_out, d_ff_1_q);
  and and_15 (and_15_out, not_15_out, d_ff_2_q);
  and and_16 (and_16_out, d_ff_3_q, not_16_out);
  or or_2 (A_2, and_1_out, not_17_out, and_2_out);
  or or_3 (B_2, and_3_out, and_4_out, d_ff_3_q);
  or or_4 (D_2, and_5_out, and_6_out, and_7_out, and_8_out);
  or or_5 (E_2, and_9_out, and_10_out);
  or or_6 (F_2, and_11_out, and_12_out, and_13_out);
  or or_7 (G_2, and_14_out, and_15_out, and_16_out);
  _7_Segment_Display u_7_segment_display_1 (.g(G_2), .f(F_2), .a(A_2), .b(B_2), .e(E_2), .d(D_2), .c(C_2));  // open: dp
  Clock clock_1 (.out(clock_1_out));
  D_Flip_Flop d_ff_4 (.clk(clock_1_out), .D(d_ff_4_qn), .Q(d_ff_4_q), .Qn(d_ff_4_qn));  // open: preset, en, reset
  D_Flip_Flop d_ff_5 (.clk(d_ff_4_qn), .D(d_ff_5_qn), .Q(d_ff_5_q), .Qn(d_ff_5_qn));  // open: preset, en, reset
  D_Flip_Flop d_ff_6 (.clk(d_ff_5_qn), .D(d_ff_6_qn), .Q(d_ff_6_q), .Qn(d_ff_6_qn));  // open: preset, en, reset
  not not_18 (not_18_out, d_ff_6_q);
  not not_19 (not_19_out, d_ff_4_q);
  not not_20 (not_20_out, d_ff_5_q);
  not not_21 (not_21_out, d_ff_4_q);
  not not_22 (not_22_out, d_ff_6_q);
  not not_23 (not_23_out, d_ff_4_q);
  not not_24 (not_24_out, d_ff_5_q);
  not not_25 (not_25_out, d_ff_6_q);
  not not_26 (not_26_out, d_ff_4_q);
  not not_27 (not_27_out, d_ff_5_q);
  not not_28 (not_28_out, d_ff_5_q);
  not not_29 (not_29_out, d_ff_6_q);
  not not_30 (not_30_out, d_ff_6_q);
  not not_31 (not_31_out, d_ff_6_q);
  not not_32 (not_32_out, d_ff_6_q);
  not not_33 (not_33_out, d_ff_5_q);
  and and_17 (and_17_out, not_18_out, not_19_out);
  or or_8 (A, and_17_out, not_34_out, and_18_out);
  not not_34 (not_34_out, d_ff_5_q);
  and and_18 (and_18_out, d_ff_6_q, d_ff_4_q);
  and and_19 (and_19_out, not_20_out, not_21_out);
  and and_20 (and_20_out, d_ff_5_q, d_ff_4_q);
  or or_9 (B, and_19_out, and_20_out, d_ff_6_q);
  or or_10 (C, not_22_out, not_23_out, d_ff_5_q);
  and and_21 (and_21_out, not_24_out, d_ff_4_q);
  and and_22 (and_22_out, not_25_out, d_ff_5_q, not_26_out);
  and and_23 (and_23_out, d_ff_6_q, not_27_out);
  and and_24 (and_24_out, d_ff_6_q, d_ff_4_q);
  and and_25 (and_25_out, not_28_out, d_ff_4_q);
  or or_11 (E, and_25_out, and_26_out);
  and and_26 (and_26_out, d_ff_6_q, d_ff_4_q);
  and and_27 (and_27_out, not_29_out, d_ff_4_q);
  and and_28 (and_28_out, not_30_out, d_ff_5_q);
  or or_12 (F, and_27_out, and_28_out, and_29_out);
  and and_29 (and_29_out, d_ff_5_q, d_ff_4_q);
  and and_30 (and_30_out, not_31_out, d_ff_4_q);
  or or_13 (G, and_30_out, and_31_out, and_32_out);
  and and_31 (and_31_out, not_32_out, d_ff_5_q);
  and and_32 (and_32_out, d_ff_6_q, not_33_out);
  or or_14 (D, and_21_out, and_22_out, and_23_out, and_24_out);
  _7_Segment_Display u_7_segment_display_2 (.g(G), .f(F), .a(A), .b(B), .e(E), .d(D), .c(C));  // open: dp

  // Notes on the sheet:
  //   C
  //   B
  //   A
  //   A
  //   C
  //   B
  //   C
  //   B
  //   A
endmodule

module counter (
);

  wire clock_1_out, d_ff_1_q, d_ff_1_qn, d_ff_2_q, d_ff_2_qn, d_ff_3_q, d_ff_3_qn;

  Clock clock_1 (.out(clock_1_out));
  D_Flip_Flop d_ff_1 (.clk(clock_1_out), .D(d_ff_1_qn), .Q(d_ff_1_q), .Qn(d_ff_1_qn));  // open: preset, en, reset
  D_Flip_Flop d_ff_2 (.clk(d_ff_1_qn), .D(d_ff_2_qn), .Q(d_ff_2_q), .Qn(d_ff_2_qn));  // open: preset, en, reset
  D_Flip_Flop d_ff_3 (.clk(d_ff_2_qn), .D(d_ff_3_qn), .Q(d_ff_3_q), .Qn(d_ff_3_qn));  // open: preset, en, reset

  // Notes on the sheet:
  //   C
  //   B
  //   A
endmodule

module display (
  input  a,
  input  b,
  input  c,
  output A_2,
  output B_2,
  output C_2,
  output D,
  output E,
  output F,
  output G
);

  wire and_1_out, and_2_out, and_3_out, and_4_out, and_5_out, and_6_out, and_7_out, and_8_out, and_9_out,
       and_10_out, and_11_out, and_12_out, and_13_out, and_14_out, and_15_out, and_16_out, not_1_out,
       not_2_out, not_3_out, not_4_out, not_5_out, not_6_out, not_7_out, not_8_out, not_9_out, not_10_out,
       not_11_out, not_12_out, not_13_out, not_14_out, not_15_out, not_16_out, not_17_out;

  not not_1 (not_1_out, a);
  not not_2 (not_2_out, c);
  not not_3 (not_3_out, b);
  not not_4 (not_4_out, c);
  not not_5 (not_5_out, a);
  not not_6 (not_6_out, c);
  not not_7 (not_7_out, b);
  not not_8 (not_8_out, a);
  not not_9 (not_9_out, c);
  not not_10 (not_10_out, b);
  not not_11 (not_11_out, b);
  not not_12 (not_12_out, a);
  not not_13 (not_13_out, a);
  not not_14 (not_14_out, a);
  not not_15 (not_15_out, a);
  not not_16 (not_16_out, b);
  and and_1 (and_1_out, not_1_out, not_2_out);
  not not_17 (not_17_out, b);
  and and_2 (and_2_out, a, c);
  and and_3 (and_3_out, not_3_out, not_4_out);
  and and_4 (and_4_out, b, c);
  or or_1 (C_2, not_5_out, not_6_out, b);
  and and_5 (and_5_out, not_7_out, c);
  and and_6 (and_6_out, not_8_out, b, not_9_out);
  and and_7 (and_7_out, a, not_10_out);
  and and_8 (and_8_out, a, c);
  and and_9 (and_9_out, not_11_out, c);
  and and_10 (and_10_out, a, c);
  and and_11 (and_11_out, not_12_out, c);
  and and_12 (and_12_out, not_13_out, b);
  and and_13 (and_13_out, b, c);
  and and_14 (and_14_out, not_14_out, c);
  and and_15 (and_15_out, not_15_out, b);
  and and_16 (and_16_out, a, not_16_out);
  or or_2 (A_2, and_1_out, not_17_out, and_2_out);
  or or_3 (B_2, and_3_out, and_4_out, a);
  or or_4 (D, and_5_out, and_6_out, and_7_out, and_8_out);
  or or_5 (E, and_9_out, and_10_out);
  or or_6 (F, and_11_out, and_12_out, and_13_out);
  or or_7 (G, and_14_out, and_15_out, and_16_out);
endmodule
