// Logisim project Midterm.circ as structural Verilog: 5 circuits, main circuit main
module main (
  input  a,
  input  b,
  input  c,
  input  d,
  output A_2,
  output A_3,
  output B_2,
  output A_4,
  output A_5,
  output B_3,
  output C_2,
  output D_2,
  output B_4,
  output C_3,
  output E,
  output F,
  output C_4,
  output B_5,
  output D_3,
  output G,
  output D_4,
  output E_2,
  output C_5,
  output F_2,
  output E_3,
  output G_2,
  output F_3,
  output D_5,
  output G_3,
  output E_4,
  output F_4,
  output G_4
);

  wire and_1_out, and_2_out, and_3_out, and_4_out, and_5_out, and_6_out, and_7_out, and_8_out, and_9_out,
       and_10_out, and_11_out, and_12_out, and_13_out, and_14_out, and_15_out, and_16_out, and_17_out,
       and_18_out, and_19_out, and_20_out, and_21_out, and_22_out, and_23_out, and_24_out, and_25_out,
       and_26_out, and_27_out, and_28_out, and_29_out, and_30_out, and_31_out, and_32_out, and_33_out,
       and_34_out, and_35_out, and_36_out, and_37_out, and_38_out, and_39_out, and_40_out, and_41_out,
       and_42_out, and_43_out, and_44_out, and_45_out, and_46_out, and_47_out, and_48_out, and_49_out,
       and_50_out, and_51_out, and_52_out, and_53_out, and_54_out, and_55_out, and_56_out, and_57_out,
       and_58_out, and_59_out, and_60_out, and_61_out, and_62_out, and_63_out, and_64_out, and_65_out,
       and_66_out, and_67_out, and_68_out, and_69_out, and_70_out, and_71_out, and_72_out, and_73_out,
       and_74_out, and_75_out, and_76_out, and_77_out, and_78_out, and_79_out, and_80_out, nand_1_out,
       nand_2_out, nand_3_out, nand_4_out, nand_5_out, nand_6_out, nand_7_out, nand_8_out, nand_9_out,
       nand_10_out, nand_11_out, nand_12_out, nand_13_out, nand_14_out, nand_15_out, nand_16_out,
       nand_17_out, nand_18_out, nand_19_out, nand_20_out, nand_21_out, nand_22_out, nand_23_out,
       nand_24_out, nand_25_out, nand_26_out, nand_27_out, nand_28_out, nand_29_out, nand_30_out,
       nand_31_out, nand_32_out, nand_33_out, nand_34_out, nand_35_out, nand_36_out, nand_37_out,
       nand_38_out, nand_39_out, nand_40_out, nand_41_out, nand_42_out, nand_43_out, nand_44_out,
       nand_45_out, nand_46_out, nand_47_out, nand_48_out, nand_49_out, nand_50_out, nand_51_out,
       nand_52_out, nand_53_out, nand_54_out, nand_55_out, nand_56_out, nand_57_out, nand_58_out,
       nand_59_out, nand_60_out, nand_61_out, nand_62_out, nand_63_out, nand_64_out, nand_65_out,
       nand_66_out, nand_67_out, nand_68_out, nand_69_out, nand_70_out, nand_71_out, nand_72_out,
       nand_73_out, nand_74_out, nand_75_out, nand_76_out, nand_77_out, nand_78_out, nand_79_out,
       nand_80_out, nand_81_out, nand_82_out, nand_83_out, nand_84_out, nand_85_out, nand_86_out,
       nand_87_out, not_1_out, not_2_out, not_3_out, not_4_out, not_5_out, not_6_out, not_7_out, not_8_out,
       not_9_out, not_10_out, not_11_out, not_12_out, not_13_out, not_14_out, not_15_out, not_16_out,
       not_17_out, not_18_out, not_19_out, not_20_out, not_21_out, not_22_out, not_23_out, not_24_out,
       not_25_out, not_26_out, not_27_out, not_28_out, not_29_out, not_30_out, not_31_out, not_32_out,
       not_33_out, not_34_out, not_35_out, not_36_out, not_37_out, not_38_out, not_39_out, not_40_out,
       not_41_out, not_42_out, not_43_out, not_44_out, not_45_out, not_46_out, not_47_out, not_48_out,
       not_49_out, not_50_out, not_51_out, not_52_out, not_53_out, not_54_out, not_55_out, not_56_out,
       not_57_out, not_58_out, not_59_out, not_60_out, not_61_out, not_62_out, not_63_out, not_64_out,
       not_65_out, not_66_out, not_67_out, not_68_out, not_69_out, not_70_out, not_71_out, not_72_out,
       not_73_out, not_74_out, not_75_out, not_76_out, not_77_out, not_78_out, not_79_out, not_80_out,
       not_81_out, not_82_out, not_83_out, not_84_out, not_85_out, not_86_out, not_87_out, not_88_out,
       not_89_out, not_90_out, not_91_out, not_92_out, not_93_out, not_94_out, not_95_out, not_96_out,
       not_97_out, not_98_out, not_99_out, not_100_out, not_101_out, not_102_out, not_103_out, not_104_out,
       not_105_out, not_106_out, not_107_out, not_108_out, not_109_out, not_110_out, not_111_out, not_112_out;

  nand nand_1 (nand_1_out, a, a);
  nand nand_2 (nand_2_out, b, b);
  nand nand_3 (nand_3_out, c, c);
  nand nand_4 (nand_4_out, a, a);
  nand nand_5 (nand_5_out, d, d);
  nand nand_6 (nand_6_out, d, d);
  nand nand_7 (nand_7_out, a, a);
  nand nand_8 (nand_8_out, b, b);
  nand nand_9 (nand_9_out, c, c);
  nand nand_10 (nand_10_out, a, a);
  nand nand_11 (nand_11_out, b, b);
  nand nand_12 (nand_12_out, a, a);
  nand nand_13 (nand_13_out, b, b);
  nand nand_14 (nand_14_out, c, c);
  nand nand_15 (nand_15_out, d, d);
  nand nand_16 (nand_16_out, c, c);
  nand nand_17 (nand_17_out, d, d);
  nand nand_18 (nand_18_out, a, a);
  nand nand_19 (nand_19_out, c, c);
  nand nand_20 (nand_20_out, d, d);
  nand nand_21 (nand_21_out, d, d);
  nand nand_22 (nand_22_out, a, a);
  nand nand_23 (nand_23_out, b, b);
  nand nand_24 (nand_24_out, d, d);
  nand nand_25 (nand_25_out, b, b);
  nand nand_26 (nand_26_out, c, c);
  nand nand_27 (nand_27_out, c, c);
  nand nand_28 (nand_28_out, d, d);
  nand nand_29 (nand_29_out, c, c);
  nand nand_30 (nand_30_out, b, b);
  nand nand_31 (nand_31_out, d, d);
  nand nand_32 (nand_32_out, a, a);
  nand nand_33 (nand_33_out, d, d);
  nand nand_34 (nand_34_out, b, b);
  nand nand_35 (nand_35_out, c, c);
  nand nand_36 (nand_36_out, d, d);
  nand nand_37 (nand_37_out, a, a);
  nand nand_38 (nand_38_out, c, c);
  nand nand_39 (nand_39_out, b, b);
  nand nand_40 (nand_40_out, b, b);
  nand nand_41 (nand_41_out, c, c);
  nand nand_42 (nand_42_out, d, d);
  nand nand_43 (nand_43_out, a, a);
  nand nand_44 (nand_44_out, a, a);
  nand nand_45 (nand_45_out, b, b);
  nand nand_46 (nand_46_out, c, c);
  nand nand_47 (nand_47_out, a, a);
  nand nand_48 (nand_48_out, b, b);
  nand nand_49 (nand_49_out, d, d);
  nand nand_50 (nand_50_out, a, a);
  nand nand_51 (nand_51_out, b, b);
  nand nand_52 (nand_52_out, c, c);
  nand nand_53 (nand_53_out, nand_1_out, nand_2_out, nand_3_out);
  nand nand_54 (nand_54_out, nand_4_out, nand_5_out);
  nand nand_55 (nand_55_out, b, nand_6_out);
  nand nand_56 (nand_56_out, nand_7_out, b, c);
  nand nand_57 (nand_57_out, a, nand_8_out, c, d);
  nand nand_58 (nand_58_out, a, b, nand_9_out);
  nand nand_59 (nand_59_out, nand_10_out, nand_11_out, c);
  nand nand_60 (nand_60_out, nand_12_out, c, d);
  nand nand_61 (nand_61_out, nand_13_out, c, d);
  nand nand_62 (nand_62_out, b, nand_14_out, nand_15_out);
  nand nand_63 (nand_63_out, a, b, nand_16_out);
  nand nand_64 (nand_64_out, a, b, nand_17_out);
  nand nand_65 (nand_65_out, nand_18_out, c, d);
  nand nand_66 (nand_66_out, b, nand_19_out, nand_20_out);
  nand nand_67 (nand_67_out, a, b, nand_21_out);
  nand nand_68 (nand_68_out, nand_22_out, nand_23_out, nand_24_out);
  nand nand_69 (nand_69_out, nand_25_out, nand_26_out);
  nand nand_70 (nand_70_out, nand_27_out, nand_28_out);
  nand nand_71 (nand_71_out, a, nand_29_out);
  nand nand_72 (nand_72_out, a, nand_30_out, d);
  nand nand_73 (nand_73_out, a, b, nand_31_out);
  nand nand_74 (nand_74_out, nand_32_out, nand_33_out);
  nand nand_75 (nand_75_out, nand_34_out, nand_35_out);
  nand nand_76 (nand_76_out, b, nand_36_out);
  nand nand_77 (nand_77_out, nand_37_out, b, c);
  nand nand_78 (nand_78_out, a, nand_38_out);
  nand nand_79 (nand_79_out, a, nand_39_out, d);
  nand nand_80 (nand_80_out, nand_40_out, nand_41_out);
  nand nand_81 (nand_81_out, b, nand_42_out);
  nand nand_82 (nand_82_out, nand_43_out, b, c);
  nand nand_83 (nand_83_out, nand_44_out, nand_45_out, nand_46_out);
  nand nand_84 (nand_84_out, nand_47_out, nand_48_out, nand_49_out);
  nand nand_85 (nand_85_out, nand_50_out, b, c);
  nand nand_86 (nand_86_out, a, nand_51_out, c, d);
  nand nand_87 (nand_87_out, a, b, nand_52_out, d);
  nand nand_88 (A_5, nand_53_out, nand_54_out, nand_55_out, nand_56_out, nand_57_out, nand_58_out);
  nand nand_89 (B_5, nand_59_out, nand_60_out, nand_61_out, nand_62_out, nand_63_out, nand_64_out);
  nand nand_90 (C_5, nand_65_out, nand_66_out, nand_67_out);
  nand nand_91 (D_5, nand_68_out, nand_69_out, nand_70_out, nand_71_out, nand_72_out, nand_73_out);
  nand nand_92 (E_4, nand_74_out, nand_75_out, nand_76_out, nand_77_out, nand_78_out, nand_79_out);
  nand nand_93 (F_4, nand_80_out, nand_81_out, nand_82_out);
  nand nand_94 (G_4, nand_83_out, nand_84_out, nand_85_out, nand_86_out, nand_87_out);
  _7_Segment_Display u_7_segment_display_1 (.g(G_4), .f(F_4), .a(A_5), .b(B_5), .e(E_4), .d(D_5), .c(C_5));  // open: dp
  not not_1 (not_1_out, a);
  not not_2 (not_2_out, d);
  not not_3 (not_3_out, a);
  not not_4 (not_4_out, b);
  not not_5 (not_5_out, a);
  not not_6 (not_6_out, d);
  not not_7 (not_7_out, b);
  not not_8 (not_8_out, c);
  not not_9 (not_9_out, c);
  not not_10 (not_10_out, a);
  not not_11 (not_11_out, b);
  not not_12 (not_12_out, c);
  not not_13 (not_13_out, b);
  not not_14 (not_14_out, d);
  not not_15 (not_15_out, c);
  not not_16 (not_16_out, b);
  not not_17 (not_17_out, c);
  not not_18 (not_18_out, d);
  not not_19 (not_19_out, a);
  not not_20 (not_20_out, a);
  not not_21 (not_21_out, c);
  not not_22 (not_22_out, d);
  not not_23 (not_23_out, b);
  not not_24 (not_24_out, b);
  not not_25 (not_25_out, c);
  not not_26 (not_26_out, d);
  not not_27 (not_27_out, a);
  not not_28 (not_28_out, a);
  not not_29 (not_29_out, d);
  not not_30 (not_30_out, b);
  not not_31 (not_31_out, d);
  not not_32 (not_32_out, c);
  not not_33 (not_33_out, d);
  not not_34 (not_34_out, a);
  not not_35 (not_35_out, b);
  and and_1 (and_1_out, not_34_out, not_35_out, not_36_out);
  not not_36 (not_36_out, c);
  not not_37 (not_37_out, a);
  not not_38 (not_38_out, b);
  and and_2 (and_2_out, not_37_out, not_38_out, d);
  not not_39 (not_39_out, a);
  not not_40 (not_40_out, c);
  and and_3 (and_3_out, not_39_out, not_40_out, d);
  and and_4 (and_4_out, not_1_out, b, c, not_2_out);
  and and_5 (and_5_out, a, not_41_out, c);
  not not_41 (not_41_out, b);
  and and_6 (and_6_out, a, b, not_42_out);
  not not_42 (not_42_out, c);
  and and_7 (and_7_out, a, b, d);
  and and_8 (and_8_out, not_3_out, not_4_out, d);
  and and_9 (and_9_out, not_5_out, c, not_6_out);
  and and_10 (and_10_out, not_7_out, c);
  and and_11 (and_11_out, a, b, not_8_out);
  not not_43 (not_43_out, a);
  and and_12 (and_12_out, not_43_out, c, not_44_out);
  not not_44 (not_44_out, d);
  not not_45 (not_45_out, b);
  and and_13 (and_13_out, not_45_out, c, d);
  and and_14 (and_14_out, a, b, not_9_out, d);
  and and_15 (and_15_out, not_10_out, not_11_out, not_12_out);
  and and_16 (and_16_out, c, d);
  and and_17 (and_17_out, a, not_13_out, not_14_out);
  and and_18 (and_18_out, a, b, not_15_out);
  and and_19 (and_19_out, not_16_out, not_17_out, not_18_out);
  and and_20 (and_20_out, not_19_out, d);
  and and_21 (and_21_out, b, d);
  and and_22 (and_22_out, not_20_out, b, c);
  and and_23 (and_23_out, a, not_21_out, not_22_out);
  and and_24 (and_24_out, a, not_23_out, c);
  and and_25 (and_25_out, not_24_out, not_25_out, not_26_out);
  and and_26 (and_26_out, c, d);
  and and_27 (and_27_out, b, d);
  and and_28 (and_28_out, not_27_out, b, c);
  not not_46 (not_46_out, a);
  and and_29 (and_29_out, not_46_out, not_47_out, not_48_out);
  not not_47 (not_47_out, b);
  not not_48 (not_48_out, c);
  not not_49 (not_49_out, a);
  not not_50 (not_50_out, c);
  and and_30 (and_30_out, not_49_out, not_50_out, d);
  and and_31 (and_31_out, not_28_out, b, c, not_29_out);
  and and_32 (and_32_out, a, not_30_out, c, not_31_out);
  and and_33 (and_33_out, a, b, not_32_out, not_33_out);
  and and_34 (and_34_out, a, b, c, d);
  or or_1 (B_4, and_8_out, and_9_out, and_10_out, and_11_out);
  or or_2 (C_4, and_12_out, and_13_out, and_14_out);
  or or_3 (D_4, and_15_out, and_16_out, and_17_out, and_18_out);
  or or_4 (E_3, and_19_out, and_20_out, and_21_out, and_22_out, and_23_out, and_24_out);
  or or_5 (F_3, and_25_out, and_26_out, and_27_out, and_28_out);
  or or_6 (A_4, and_1_out, and_2_out, and_3_out, and_4_out, and_5_out, and_6_out, and_7_out);
  or or_7 (G_3, and_29_out, and_30_out, and_31_out, and_32_out, and_33_out, and_34_out);
  _7_Segment_Display u_7_segment_display_2 (.g(G_3), .f(F_3), .a(A_4), .b(B_4), .e(E_3), .d(D_4), .c(C_4));  // open: dp
  not not_51 (not_51_out, b);
  and and_35 (and_35_out, not_51_out, not_52_out);
  not not_52 (not_52_out, d);
  and and_36 (and_36_out, b, not_53_out);
  not not_53 (not_53_out, c);
  not not_54 (not_54_out, b);
  and and_37 (and_37_out, not_54_out, not_55_out);
  not not_55 (not_55_out, d);
  not not_56 (not_56_out, c);
  and and_38 (and_38_out, not_56_out, d);
  and and_39 (and_39_out, a, not_57_out);
  not not_57 (not_57_out, b);
  and and_40 (and_40_out, a, not_58_out);
  not not_58 (not_58_out, c);
  not not_59 (not_59_out, a);
  and and_41 (and_41_out, not_59_out, not_60_out, d);
  not not_60 (not_60_out, c);
  not not_61 (not_61_out, b);
  and and_42 (and_42_out, not_61_out, c, not_62_out);
  not not_62 (not_62_out, d);
  and and_43 (and_43_out, a, not_63_out, not_64_out);
  not not_63 (not_63_out, c);
  not not_64 (not_64_out, d);
  not not_65 (not_65_out, b);
  and and_44 (and_44_out, not_65_out, not_66_out);
  not not_66 (not_66_out, d);
  and and_45 (and_45_out, b, c);
  not not_67 (not_67_out, d);
  or or_8 (E, not_67_out, b, a);
  and and_46 (and_46_out, c, not_68_out);
  not not_68 (not_68_out, d);
  not not_69 (not_69_out, a);
  and and_47 (and_47_out, not_69_out, not_70_out, not_71_out);
  not not_70 (not_70_out, c);
  not not_71 (not_71_out, d);
  not not_72 (not_72_out, a);
  and and_48 (and_48_out, not_72_out, b, not_73_out);
  not not_73 (not_73_out, c);
  and and_49 (and_49_out, a, d);
  and and_50 (and_50_out, a, b, c);
  or or_9 (A_2, and_35_out, and_36_out, a);
  or or_10 (B_2, and_37_out, and_38_out, and_39_out, and_40_out);
  or or_11 (C_2, and_41_out, and_42_out, and_43_out);
  or or_12 (D_2, and_44_out, and_45_out, a);
  or or_13 (F, and_46_out, b);
  or or_14 (G, and_47_out, and_48_out, and_49_out, and_50_out);
  _7_Segment_Display u_7_segment_display_3 (.g(G), .f(F), .a(A_2), .b(B_2), .e(E), .d(D_2), .c(C_2));  // open: dp
  not not_74 (not_74_out, b);
  not not_75 (not_75_out, a);
  not not_76 (not_76_out, c);
  not not_77 (not_77_out, d);
  not not_78 (not_78_out, b);
  not not_79 (not_79_out, a);
  not not_80 (not_80_out, c);
  not not_81 (not_81_out, d);
  not not_82 (not_82_out, b);
  not not_83 (not_83_out, c);
  not not_84 (not_84_out, b);
  not not_85 (not_85_out, a);
  not not_86 (not_86_out, b);
  not not_87 (not_87_out, c);
  not not_88 (not_88_out, a);
  not not_89 (not_89_out, c);
  not not_90 (not_90_out, d);
  not not_91 (not_91_out, b);
  not not_92 (not_92_out, c);
  not not_93 (not_93_out, d);
  not not_94 (not_94_out, b);
  not not_95 (not_95_out, b);
  not not_96 (not_96_out, c);
  not not_97 (not_97_out, a);
  not not_98 (not_98_out, d);
  not not_99 (not_99_out, b);
  not not_100 (not_100_out, b);
  not not_101 (not_101_out, c);
  not not_102 (not_102_out, a);
  not not_103 (not_103_out, c);
  not not_104 (not_104_out, d);
  not not_105 (not_105_out, a);
  not not_106 (not_106_out, b);
  not not_107 (not_107_out, a);
  not not_108 (not_108_out, c);
  not not_109 (not_109_out, d);
  not not_110 (not_110_out, b);
  not not_111 (not_111_out, d);
  not not_112 (not_112_out, d);
  and and_51 (and_51_out, not_74_out, d);
  and and_52 (and_52_out, not_75_out, b, not_76_out, not_77_out);
  and and_53 (and_53_out, a, not_78_out);
  and and_54 (and_54_out, a, d);
  and and_55 (and_55_out, a, c);
  and and_56 (and_56_out, not_79_out, not_80_out, not_81_out);
  and and_57 (and_57_out, not_82_out, not_83_out);
  and and_58 (and_58_out, a, not_84_out);
  and and_59 (and_59_out, a, c, d);
  and and_60 (and_60_out, not_85_out, not_86_out, not_87_out);
  and and_61 (and_61_out, not_88_out, not_89_out, not_90_out);
  and and_62 (and_62_out, a, not_91_out, d);
  and and_63 (and_63_out, not_92_out, d);
  and and_64 (and_64_out, b, c, not_93_out);
  and and_65 (and_65_out, a, not_94_out);
  and and_66 (and_66_out, a, d);
  and and_67 (and_67_out, not_95_out, d);
  and and_68 (and_68_out, not_96_out, d);
  and and_69 (and_69_out, not_97_out, b, not_98_out);
  and and_70 (and_70_out, a, not_99_out);
  and and_71 (and_71_out, a, c);
  and and_72 (and_72_out, not_100_out, d);
  and and_73 (and_73_out, not_101_out, d);
  and and_74 (and_74_out, not_102_out, b, not_103_out);
  and and_75 (and_75_out, b, c, not_104_out);
  and and_76 (and_76_out, not_105_out, not_106_out, c, d);
  and and_77 (and_77_out, not_107_out, b, not_108_out, not_109_out);
  and and_78 (and_78_out, a, not_110_out, not_111_out);
  and and_79 (and_79_out, a, c, not_112_out);
  and and_80 (and_80_out, a, b, d);
  or or_15 (A_3, and_51_out, and_52_out, and_53_out, and_54_out, and_55_out);
  or or_16 (B_3, and_56_out, and_57_out, and_58_out, and_59_out);
  or or_17 (C_3, and_60_out, and_61_out, and_62_out);
  or or_18 (D_3, and_63_out, and_64_out, and_65_out, and_66_out);
  or or_19 (E_2, and_67_out, and_68_out, and_69_out, and_70_out, and_71_out);
  or or_20 (F_2, and_72_out, and_73_out, and_74_out, and_75_out);
  or or_21 (G_2, and_76_out, and_77_out, and_78_out, and_79_out, and_80_out);
  _7_Segment_Display u_7_segment_display_4 (.g(G_2), .f(F_2), .a(A_3), .b(B_3), .e(E_2), .d(D_3), .c(C_3));  // open: dp
endmodule

module Display_1 (
  input  a,
  input  b,
  input  c,
  input  d,
  output A_2,
  output B_2,
  output C_2,
  output D_2,
  output E,
  output F,
  output G
);

  wire nand_1_out, nand_2_out, nand_3_out, nand_4_out, nand_5_out, nand_6_out, nand_7_out, nand_8_out,
       nand_9_out, nand_10_out, nand_11_out, nand_12_out, nand_13_out, nand_14_out, nand_15_out, nand_16_out,
       nand_17_out, nand_18_out, nand_19_out, nand_20_out, nand_21_out, nand_22_out, nand_23_out,
       nand_24_out, nand_25_out, nand_26_out, nand_27_out, nand_28_out, nand_29_out, nand_30_out,
       nand_31_out, nand_32_out, nand_33_out, nand_34_out, nand_35_out, nand_36_out, nand_37_out,
       nand_38_out, nand_39_out, nand_40_out, nand_41_out, nand_42_out, nand_43_out, nand_44_out,
       nand_45_out, nand_46_out, nand_47_out, nand_48_out, nand_49_out, nand_50_out, nand_51_out,
       nand_52_out, nand_53_out, nand_54_out, nand_55_out, nand_56_out, nand_57_out, nand_58_out,
       nand_59_out, nand_60_out, nand_61_out, nand_62_out, nand_63_out, nand_64_out, nand_65_out,
       nand_66_out, nand_67_out, nand_68_out, nand_69_out, nand_70_out, nand_71_out, nand_72_out,
       nand_73_out, nand_74_out, nand_75_out, nand_76_out, nand_77_out, nand_78_out, nand_79_out,
       nand_80_out, nand_81_out, nand_82_out, nand_83_out, nand_84_out, nand_85_out, nand_86_out, nand_87_out;

  nand nand_1 (nand_1_out, a, a);
  nand nand_2 (nand_2_out, b, b);
  nand nand_3 (nand_3_out, c, c);
  nand nand_4 (nand_4_out, a, a);
  nand nand_5 (nand_5_out, d, d);
  nand nand_6 (nand_6_out, d, d);
  nand nand_7 (nand_7_out, a, a);
  nand nand_8 (nand_8_out, b, b);
  nand nand_9 (nand_9_out, c, c);
  nand nand_10 (nand_10_out, a, a);
  nand nand_11 (nand_11_out, b, b);
  nand nand_12 (nand_12_out, a, a);
  nand nand_13 (nand_13_out, b, b);
  nand nand_14 (nand_14_out, c, c);
  nand nand_15 (nand_15_out, d, d);
  nand nand_16 (nand_16_out, c, c);
  nand nand_17 (nand_17_out, d, d);
  nand nand_18 (nand_18_out, a, a);
  nand nand_19 (nand_19_out, c, c);
  nand nand_20 (nand_20_out, d, d);
  nand nand_21 (nand_21_out, d, d);
  nand nand_22 (nand_22_out, a, a);
  nand nand_23 (nand_23_out, b, b);
  nand nand_24 (nand_24_out, d, d);
  nand nand_25 (nand_25_out, b, b);
  nand nand_26 (nand_26_out, c, c);
  nand nand_27 (nand_27_out, c, c);
  nand nand_28 (nand_28_out, d, d);
  nand nand_29 (nand_29_out, c, c);
  nand nand_30 (nand_30_out, b, b);
  nand nand_31 (nand_31_out, d, d);
  nand nand_32 (nand_32_out, a, a);
  nand nand_33 (nand_33_out, d, d);
  nand nand_34 (nand_34_out, b, b);
  nand nand_35 (nand_35_out, c, c);
  nand nand_36 (nand_36_out, d, d);
  nand nand_37 (nand_37_out, a, a);
  nand nand_38 (nand_38_out, c, c);
  nand nand_39 (nand_39_out, b, b);
  nand nand_40 (nand_40_out, b, b);
  nand nand_41 (nand_41_out, c, c);
  nand nand_42 (nand_42_out, d, d);
  nand nand_43 (nand_43_out, a, a);
  nand nand_44 (nand_44_out, a, a);
  nand nand_45 (nand_45_out, b, b);
  nand nand_46 (nand_46_out, c, c);
  nand nand_47 (nand_47_out, a, a);
  nand nand_48 (nand_48_out, b, b);
  nand nand_49 (nand_49_out, d, d);
  nand nand_50 (nand_50_out, a, a);
  nand nand_51 (nand_51_out, b, b);
  nand nand_52 (nand_52_out, c, c);
  nand nand_53 (nand_53_out, nand_1_out, nand_2_out, nand_3_out);
  nand nand_54 (nand_54_out, nand_4_out, nand_5_out);
  nand nand_55 (nand_55_out, b, nand_6_out);
  nand nand_56 (nand_56_out, nand_7_out, b, c);
  nand nand_57 (nand_57_out, a, nand_8_out, c, d);
  nand nand_58 (nand_58_out, a, b, nand_9_out);
  nand nand_59 (nand_59_out, nand_10_out, nand_11_out, c);
  nand nand_60 (nand_60_out, nand_12_out, c, d);
  nand nand_61 (nand_61_out, nand_13_out, c, d);
  nand nand_62 (nand_62_out, b, nand_14_out, nand_15_out);
  nand nand_63 (nand_63_out, a, b, nand_16_out);
  nand nand_64 (nand_64_out, a, b, nand_17_out);
  nand nand_65 (nand_65_out, nand_18_out, c, d);
  nand nand_66 (nand_66_out, b, nand_19_out, nand_20_out);
  nand nand_67 (nand_67_out, a, b, nand_21_out);
  nand nand_68 (nand_68_out, nand_22_out, nand_23_out, nand_24_out);
  nand nand_69 (nand_69_out, nand_25_out, nand_26_out);
  nand nand_70 (nand_70_out, nand_27_out, nand_28_out);
  nand nand_71 (nand_71_out, a, nand_29_out);
  nand nand_72 (nand_72_out, a, nand_30_out, d);
  nand nand_73 (nand_73_out, a, b, nand_31_out);
  nand nand_74 (nand_74_out, nand_32_out, nand_33_out);
  nand nand_75 (nand_75_out, nand_34_out, nand_35_out);
  nand nand_76 (nand_76_out, b, nand_36_out);
  nand nand_77 (nand_77_out, nand_37_out, b, c);
  nand nand_78 (nand_78_out, a, nand_38_out);
  nand nand_79 (nand_79_out, a, nand_39_out, d);
  nand nand_80 (nand_80_out, nand_40_out, nand_41_out);
  nand nand_81 (nand_81_out, b, nand_42_out);
  nand nand_82 (nand_82_out, nand_43_out, b, c);
  nand nand_83 (nand_83_out, nand_44_out, nand_45_out, nand_46_out);
  nand nand_84 (nand_84_out, nand_47_out, nand_48_out, nand_49_out);
  nand nand_85 (nand_85_out, nand_50_out, b, c);
  nand nand_86 (nand_86_out, a, nand_51_out, c, d);
  nand nand_87 (nand_87_out, a, b, nand_52_out, d);
  nand nand_88 (A_2, nand_53_out, nand_54_out, nand_55_out, nand_56_out, nand_57_out, nand_58_out);
  nand nand_89 (B_2, nand_59_out, nand_60_out, nand_61_out, nand_62_out, nand_63_out, nand_64_out);
  nand nand_90 (C_2, nand_65_out, nand_66_out, nand_67_out);
  nand nand_91 (D_2, nand_68_out, nand_69_out, nand_70_out, nand_71_out, nand_72_out, nand_73_out);
  nand nand_92 (E, nand_74_out, nand_75_out, nand_76_out, nand_77_out, nand_78_out, nand_79_out);
  nand nand_93 (F, nand_80_out, nand_81_out, nand_82_out);
  nand nand_94 (G, nand_83_out, nand_84_out, nand_85_out, nand_86_out, nand_87_out);
  _7_Segment_Display u_7_segment_display_1 (.g(G), .f(F), .a(A_2), .b(B_2), .e(E), .d(D_2), .c(C_2));  // open: dp
endmodule

module Display_2 (
  input  a,
  input  b,
  input  c,
  input  d,
  output A_2,
  output B_2,
  output C_2,
  output D_2,
  output E,
  output F,
  output G
);

  wire and_1_out, and_2_out, and_3_out, and_4_out, and_5_out, and_6_out, and_7_out, and_8_out, and_9_out,
       and_10_out, and_11_out, and_12_out, and_13_out, and_14_out, and_15_out, and_16_out, and_17_out,
       and_18_out, and_19_out, and_20_out, and_21_out, and_22_out, and_23_out, and_24_out, and_25_out,
       and_26_out, and_27_out, and_28_out, and_29_out, and_30_out, and_31_out, and_32_out, and_33_out,
       and_34_out, not_1_out, not_2_out, not_3_out, not_4_out, not_5_out, not_6_out, not_7_out, not_8_out,
       not_9_out, not_10_out, not_11_out, not_12_out, not_13_out, not_14_out, not_15_out, not_16_out,
       not_17_out, not_18_out, not_19_out, not_20_out, not_21_out, not_22_out, not_23_out, not_24_out,
       not_25_out, not_26_out, not_27_out, not_28_out, not_29_out, not_30_out, not_31_out, not_32_out,
       not_33_out, not_34_out, not_35_out, not_36_out, not_37_out, not_38_out, not_39_out, not_40_out,
       not_41_out, not_42_out, not_43_out, not_44_out, not_45_out, not_46_out, not_47_out, not_48_out,
       not_49_out, not_50_out;

  not not_1 (not_1_out, a);
  not not_2 (not_2_out, b);
  not not_3 (not_3_out, c);
  not not_4 (not_4_out, a);
  not not_5 (not_5_out, b);
  not not_6 (not_6_out, a);
  not not_7 (not_7_out, c);
  not not_8 (not_8_out, a);
  not not_9 (not_9_out, d);
  not not_10 (not_10_out, b);
  not not_11 (not_11_out, c);
  not not_12 (not_12_out, a);
  and and_1 (and_1_out, not_12_out, not_13_out, d);
  not not_13 (not_13_out, b);
  not not_14 (not_14_out, a);
  and and_2 (and_2_out, not_14_out, c, not_15_out);
  not not_15 (not_15_out, d);
  not not_16 (not_16_out, b);
  and and_3 (and_3_out, not_16_out, c);
  and and_4 (and_4_out, a, b, not_17_out);
  not not_17 (not_17_out, c);
  not not_18 (not_18_out, a);
  not not_19 (not_19_out, d);
  not not_20 (not_20_out, b);
  not not_21 (not_21_out, c);
  not not_22 (not_22_out, a);
  not not_23 (not_23_out, b);
  and and_5 (and_5_out, not_22_out, not_23_out, not_24_out);
  not not_24 (not_24_out, c);
  and and_6 (and_6_out, c, d);
  and and_7 (and_7_out, a, not_25_out, not_26_out);
  not not_25 (not_25_out, b);
  not not_26 (not_26_out, d);
  and and_8 (and_8_out, a, b, not_27_out);
  not not_27 (not_27_out, c);
  not not_28 (not_28_out, b);
  not not_29 (not_29_out, c);
  and and_9 (and_9_out, not_28_out, not_29_out, not_30_out);
  not not_30 (not_30_out, d);
  not not_31 (not_31_out, a);
  and and_10 (and_10_out, not_31_out, d);
  and and_11 (and_11_out, b, d);
  not not_32 (not_32_out, a);
  and and_12 (and_12_out, not_32_out, b, c);
  and and_13 (and_13_out, a, not_33_out, not_34_out);
  not not_33 (not_33_out, c);
  not not_34 (not_34_out, d);
  not not_35 (not_35_out, b);
  and and_14 (and_14_out, a, not_35_out, c);
  not not_36 (not_36_out, b);
  and and_15 (and_15_out, not_36_out, not_37_out, not_38_out);
  not not_37 (not_37_out, c);
  not not_38 (not_38_out, d);
  and and_16 (and_16_out, c, d);
  and and_17 (and_17_out, b, d);
  not not_39 (not_39_out, a);
  and and_18 (and_18_out, not_39_out, b, c);
  not not_40 (not_40_out, a);
  not not_41 (not_41_out, b);
  not not_42 (not_42_out, c);
  not not_43 (not_43_out, a);
  not not_44 (not_44_out, c);
  not not_45 (not_45_out, a);
  not not_46 (not_46_out, d);
  not not_47 (not_47_out, b);
  not not_48 (not_48_out, d);
  not not_49 (not_49_out, c);
  not not_50 (not_50_out, d);
  and and_19 (and_19_out, not_1_out, not_2_out, not_3_out);
  and and_20 (and_20_out, not_4_out, not_5_out, d);
  and and_21 (and_21_out, not_6_out, not_7_out, d);
  and and_22 (and_22_out, not_8_out, b, c, not_9_out);
  and and_23 (and_23_out, a, not_10_out, c);
  and and_24 (and_24_out, a, b, not_11_out);
  and and_25 (and_25_out, a, b, d);
  or or_1 (B_2, and_1_out, and_2_out, and_3_out, and_4_out);
  and and_26 (and_26_out, not_18_out, c, not_19_out);
  and and_27 (and_27_out, not_20_out, c, d);
  or or_2 (C_2, and_26_out, and_27_out, and_28_out);
  and and_28 (and_28_out, a, b, not_21_out, d);
  or or_3 (D_2, and_5_out, and_6_out, and_7_out, and_8_out);
  or or_4 (F, and_15_out, and_16_out, and_17_out, and_18_out);
  and and_29 (and_29_out, not_40_out, not_41_out, not_42_out);
  and and_30 (and_30_out, not_43_out, not_44_out, d);
  and and_31 (and_31_out, not_45_out, b, c, not_46_out);
  and and_32 (and_32_out, a, not_47_out, c, not_48_out);
  and and_33 (and_33_out, a, b, not_49_out, not_50_out);
  and and_34 (and_34_out, a, b, c, d);
  or or_5 (A_2, and_19_out, and_20_out, and_21_out, and_22_out, and_23_out, and_24_out, and_25_out);
  or or_6 (E, and_9_out, and_10_out, and_11_out, and_12_out, and_13_out, and_14_out);
  or or_7 (G, and_29_out, and_30_out, and_31_out, and_32_out, and_33_out, and_34_out);
  _7_Segment_Display u_7_segment_display_1 (.g(G), .f(F), .a(A_2), .b(B_2), .e(E), .d(D_2), .c(C_2));  // open: dp
endmodule

module Display_3 (
  input  a,
  input  b,
  input  c,
  input  d,
  output A_2,
  output B_2,
  output C_2,
  output D_2,
  output E,
  output F,
  output G
);

  wire and_1_out, and_2_out, and_3_out, and_4_out, and_5_out, and_6_out, and_7_out, and_8_out, and_9_out,
       and_10_out, and_11_out, and_12_out, and_13_out, and_14_out, and_15_out, and_16_out, not_1_out,
       not_2_out, not_3_out, not_4_out, not_5_out, not_6_out, not_7_out, not_8_out, not_9_out, not_10_out,
       not_11_out, not_12_out, not_13_out, not_14_out, not_15_out, not_16_out, not_17_out, not_18_out,
       not_19_out, not_20_out, not_21_out, not_22_out, not_23_out;

  not not_1 (not_1_out, b);
  and and_1 (and_1_out, not_1_out, not_2_out);
  not not_2 (not_2_out, d);
  and and_2 (and_2_out, b, not_3_out);
  not not_3 (not_3_out, c);
  not not_4 (not_4_out, b);
  and and_3 (and_3_out, not_4_out, not_5_out);
  not not_5 (not_5_out, d);
  not not_6 (not_6_out, c);
  and and_4 (and_4_out, not_6_out, d);
  and and_5 (and_5_out, a, not_7_out);
  not not_7 (not_7_out, b);
  and and_6 (and_6_out, a, not_8_out);
  not not_8 (not_8_out, c);
  not not_9 (not_9_out, a);
  and and_7 (and_7_out, not_9_out, not_10_out, d);
  not not_10 (not_10_out, c);
  not not_11 (not_11_out, b);
  and and_8 (and_8_out, not_11_out, c, not_12_out);
  not not_12 (not_12_out, d);
  not not_13 (not_13_out, c);
  and and_9 (and_9_out, a, not_13_out, not_14_out);
  not not_14 (not_14_out, d);
  not not_15 (not_15_out, b);
  and and_10 (and_10_out, not_15_out, not_16_out);
  not not_16 (not_16_out, d);
  and and_11 (and_11_out, b, c);
  not not_17 (not_17_out, d);
  or or_1 (E, not_17_out, b, a);
  and and_12 (and_12_out, c, not_18_out);
  not not_18 (not_18_out, d);
  not not_19 (not_19_out, a);
  and and_13 (and_13_out, not_19_out, not_20_out, not_21_out);
  not not_20 (not_20_out, c);
  not not_21 (not_21_out, d);
  not not_22 (not_22_out, a);
  and and_14 (and_14_out, not_22_out, b, not_23_out);
  not not_23 (not_23_out, c);
  and and_15 (and_15_out, a, d);
  and and_16 (and_16_out, a, b, c);
  or or_2 (A_2, and_1_out, and_2_out, a);
  or or_3 (B_2, and_3_out, and_4_out, and_5_out, and_6_out);
  or or_4 (C_2, and_7_out, and_8_out, and_9_out);
  or or_5 (D_2, and_10_out, and_11_out, a);
  or or_6 (F, and_12_out, b);
  or or_7 (G, and_13_out, and_14_out, and_15_out, and_16_out);
  _7_Segment_Display u_7_segment_display_1 (.g(G), .f(F), .a(A_2), .b(B_2), .e(E), .d(D_2), .c(C_2));  // open: dp
endmodule

module Display_4 (
  input  a,
  input  b,
  input  c,
  input  d,
  output A_2,
  output B_2,
  output C_2,
  output D_2,
  output E,
  output F,
  output G
);

  wire and_1_out, and_2_out, and_3_out, and_4_out, and_5_out, and_6_out, and_7_out, and_8_out, and_9_out,
       and_10_out, and_11_out, and_12_out, and_13_out, and_14_out, and_15_out, and_16_out, and_17_out,
       and_18_out, and_19_out, and_20_out, and_21_out, and_22_out, and_23_out, and_24_out, and_25_out,
       and_26_out, and_27_out, and_28_out, and_29_out, and_30_out, not_1_out, not_2_out, not_3_out,
       not_4_out, not_5_out, not_6_out, not_7_out, not_8_out, not_9_out, not_10_out, not_11_out, not_12_out,
       not_13_out, not_14_out, not_15_out, not_16_out, not_17_out, not_18_out, not_19_out, not_20_out,
       not_21_out, not_22_out, not_23_out, not_24_out, not_25_out, not_26_out, not_27_out, not_28_out,
       not_29_out, not_30_out, not_31_out, not_32_out, not_33_out, not_34_out, not_35_out, not_36_out,
       not_37_out, not_38_out, not_39_out;

  not not_1 (not_1_out, b);
  not not_2 (not_2_out, a);
  not not_3 (not_3_out, c);
  not not_4 (not_4_out, d);
  not not_5 (not_5_out, b);
  not not_6 (not_6_out, a);
  and and_1 (and_1_out, not_6_out, not_7_out, not_8_out);
  not not_7 (not_7_out, c);
  not not_8 (not_8_out, d);
  not not_9 (not_9_out, b);
  and and_2 (and_2_out, not_9_out, not_10_out);
  not not_10 (not_10_out, c);
  and and_3 (and_3_out, a, not_11_out);
  not not_11 (not_11_out, b);
  and and_4 (and_4_out, a, c, d);
  not not_12 (not_12_out, a);
  and and_5 (and_5_out, not_12_out, not_13_out, not_14_out);
  not not_13 (not_13_out, b);
  not not_14 (not_14_out, c);
  not not_15 (not_15_out, a);
  and and_6 (and_6_out, not_15_out, not_16_out, not_17_out);
  not not_16 (not_16_out, c);
  not not_17 (not_17_out, d);
  not not_18 (not_18_out, b);
  and and_7 (and_7_out, a, not_18_out, d);
  not not_19 (not_19_out, c);
  and and_8 (and_8_out, not_19_out, d);
  and and_9 (and_9_out, b, c, not_20_out);
  not not_20 (not_20_out, d);
  and and_10 (and_10_out, a, not_21_out);
  not not_21 (not_21_out, b);
  and and_11 (and_11_out, a, d);
  not not_22 (not_22_out, b);
  and and_12 (and_12_out, not_22_out, d);
  not not_23 (not_23_out, c);
  and and_13 (and_13_out, not_23_out, d);
  not not_24 (not_24_out, a);
  and and_14 (and_14_out, not_24_out, b, not_25_out);
  not not_25 (not_25_out, d);
  and and_15 (and_15_out, a, not_26_out);
  not not_26 (not_26_out, b);
  and and_16 (and_16_out, a, c);
  not not_27 (not_27_out, b);
  and and_17 (and_17_out, not_27_out, d);
  not not_28 (not_28_out, c);
  and and_18 (and_18_out, not_28_out, d);
  not not_29 (not_29_out, a);
  and and_19 (and_19_out, not_29_out, b, not_30_out);
  not not_30 (not_30_out, c);
  and and_20 (and_20_out, b, c, not_31_out);
  not not_31 (not_31_out, d);
  not not_32 (not_32_out, a);
  not not_33 (not_33_out, b);
  not not_34 (not_34_out, a);
  not not_35 (not_35_out, c);
  not not_36 (not_36_out, d);
  not not_37 (not_37_out, b);
  not not_38 (not_38_out, d);
  not not_39 (not_39_out, d);
  and and_21 (and_21_out, not_1_out, d);
  and and_22 (and_22_out, not_2_out, b, not_3_out, not_4_out);
  and and_23 (and_23_out, a, not_5_out);
  and and_24 (and_24_out, a, d);
  and and_25 (and_25_out, a, c);
  or or_1 (B_2, and_1_out, and_2_out, and_3_out, and_4_out);
  or or_2 (C_2, and_5_out, and_6_out, and_7_out);
  or or_3 (D_2, and_8_out, and_9_out, and_10_out, and_11_out);
  or or_4 (E, and_12_out, and_13_out, and_14_out, and_15_out, and_16_out);
  or or_5 (F, and_17_out, and_18_out, and_19_out, and_20_out);
  and and_26 (and_26_out, not_32_out, not_33_out, c, d);
  and and_27 (and_27_out, not_34_out, b, not_35_out, not_36_out);
  and and_28 (and_28_out, a, not_37_out, not_38_out);
  and and_29 (and_29_out, a, c, not_39_out);
  and and_30 (and_30_out, a, b, d);
  or or_6 (A_2, and_21_out, and_22_out, and_23_out, and_24_out, and_25_out);
  or or_7 (G, and_26_out, and_27_out, and_28_out, and_29_out, and_30_out);
  _7_Segment_Display u_7_segment_display_1 (.g(G), .f(F), .a(A_2), .b(B_2), .e(E), .d(D_2), .c(C_2));  // open: dp
endmodule
