// Logisim project project.circ as structural Verilog: 17 circuits, main circuit main
module main (
  input  A,
  input  B,
  input  C,
  input  D,
  input  Reset,
  input  Reset_2,
  output Tie,
  output Tie_2,
  output Lose,
  output Win,
  output Lose_2,
  output Win_2
);

  wire clock_1_out;
  wire [3:0] left_subcircuit_1_sum, right_subcircuit_1_sum;

  Clock clock_1 (.out(clock_1_out));
  Left_subcircuit left_subcircuit_1 (
    .A(A), .B(B), .C(C), .D(D), .Sum(left_subcircuit_1_sum), .Clock(clock_1_out), .Win_Tie(Tie), .Win(Win),
    .Lose(Lose), .reset(Reset));
  Hex_Digit_Display hex_digit_display_1 (.value(left_subcircuit_1_sum));  // open: dp
  Right_subcircuit right_subcircuit_1 (
    .A(A), .B(B), .C(C), .D(D), .Sum(right_subcircuit_1_sum), .Clock(clock_1_out), .Win_Tie(Tie_2),
    .Win(Win_2), .Lose(Lose_2), .reset(Reset_2));
  Hex_Digit_Display hex_digit_display_2 (.value(right_subcircuit_1_sum));  // open: dp

  // Notes on the sheet:
  //   Left player
  //   Left player score
  //   Right player
  //   Inputs: 
  //   Rock: 01
  //   Paper: 10
  //   Scissors: 11
  //   Right player score
  //   illegal: 00
endmodule

module player (
  input  A,
  input  B,
  output R,
  output P,
  output S
);

  wire not_1_out, not_2_out;

  not not_1 (not_1_out, A);
  not not_2 (not_2_out, B);
  and and_1 (S, A, B);
  and and_2 (R, not_1_out, B);
  and and_3 (P, A, not_2_out);
endmodule

module inputs (
  input  A,
  input  B,
  input  C,
  input  D,
  output W1,
  output W2,
  output Tie
);

  wire and_1_out, and_2_out, and_3_out, and_4_out, and_5_out, and_6_out, and_7_out, and_8_out, and_9_out,
       not_1_out, not_2_out, not_3_out, not_4_out, not_5_out, not_6_out, not_7_out, not_8_out, not_9_out,
       not_10_out, not_11_out, not_12_out;

  not not_1 (not_1_out, A);
  not not_2 (not_2_out, B);
  not not_3 (not_3_out, C);
  not not_4 (not_4_out, D);
  not not_5 (not_5_out, A);
  not not_6 (not_6_out, D);
  not not_7 (not_7_out, B);
  not not_8 (not_8_out, C);
  not not_9 (not_9_out, A);
  not not_10 (not_10_out, C);
  not not_11 (not_11_out, B);
  not not_12 (not_12_out, D);
  and and_1 (and_1_out, not_1_out, B, C, D);
  and and_2 (and_2_out, A, not_2_out, not_3_out, D);
  or or_1 (W1, and_1_out, and_2_out, and_3_out);
  and and_3 (and_3_out, A, B, C, not_4_out);
  and and_4 (and_4_out, not_5_out, B, C, not_6_out);
  and and_5 (and_5_out, A, not_7_out, C, D);
  or or_2 (W2, and_4_out, and_5_out, and_6_out);
  and and_6 (and_6_out, A, B, not_8_out, D);
  and and_7 (and_7_out, not_9_out, B, not_10_out, D);
  or or_3 (Tie, and_7_out, and_8_out, and_9_out);
  and and_8 (and_8_out, A, not_11_out, C, not_12_out);
  and and_9 (and_9_out, A, B, C, D);
endmodule

module _1_bit_ripple_adder (
  input  Cin,
  input  A,
  input  B,
  output Sum,
  output Cout
);

  wire and_1_out, and_2_out, xor_1_out;

  xor xor_1 (xor_1_out, A, B);
  xor xor_2 (Sum, xor_1_out, Cin);
  and and_1 (and_1_out, xor_1_out, Cin);
  and and_2 (and_2_out, A, B);
  or or_1 (Cout, and_1_out, and_2_out);
endmodule

module _4_bit_ripple_adder (
  input  [3:0] A,
  input  [3:0] B,
  output [3:0] Sum,
  output Overflow
);

  wire n1_bit_ripple_adder_1_cout, n1_bit_ripple_adder_2_cout, n1_bit_ripple_adder_3_cout;

  _1_bit_ripple_adder u_1_bit_ripple_adder_1 (
    .Cin(1'b0), .A(A[0]), .B(B[0]), .Sum(Sum[0]), .Cout(n1_bit_ripple_adder_1_cout));
  _1_bit_ripple_adder u_1_bit_ripple_adder_2 (
    .Cin(n1_bit_ripple_adder_1_cout), .A(A[1]), .B(B[1]), .Sum(Sum[1]), .Cout(n1_bit_ripple_adder_2_cout));
  _1_bit_ripple_adder u_1_bit_ripple_adder_3 (
    .Cin(n1_bit_ripple_adder_2_cout), .A(A[2]), .B(B[2]), .Sum(Sum[2]), .Cout(n1_bit_ripple_adder_3_cout));
  _1_bit_ripple_adder u_1_bit_ripple_adder_4 (
    .Cin(n1_bit_ripple_adder_3_cout), .A(A[3]), .B(B[3]), .Sum(Sum[3]), .Cout(Overflow));

  // Notes on the sheet:
  //   LSB
  //   MSB
endmodule

module _4_bit_counter (
  input  Reset,
  input  [3:0] A,
  input  Clock,
  input  [3:0] B,
  output [3:0] Sum,
  output Overflow
);

  wire n1_bit_ripple_adder_1_cout, n1_bit_ripple_adder_2_cout, n1_bit_ripple_adder_3_cout,
       n1_bit_ripple_adder_4_cout;
  wire [3:0] n1_bit_ripple_adder_1_sum;

  _1_bit_ripple_adder u_1_bit_ripple_adder_1 (
    .Cin(1'b0), .A(A[0]), .B(B[0]), .Sum(n1_bit_ripple_adder_1_sum[0]), .Cout(n1_bit_ripple_adder_1_cout));
  _1_bit_ripple_adder u_1_bit_ripple_adder_2 (
    .Cin(n1_bit_ripple_adder_1_cout), .A(A[1]), .B(B[1]), .Sum(n1_bit_ripple_adder_1_sum[1]),
    .Cout(n1_bit_ripple_adder_2_cout));
  _1_bit_ripple_adder u_1_bit_ripple_adder_3 (
    .Cin(n1_bit_ripple_adder_2_cout), .A(A[2]), .B(B[2]), .Sum(n1_bit_ripple_adder_1_sum[2]),
    .Cout(n1_bit_ripple_adder_3_cout));
  _1_bit_ripple_adder u_1_bit_ripple_adder_4 (
    .Cin(n1_bit_ripple_adder_3_cout), .A(A[3]), .B(B[3]), .Sum(n1_bit_ripple_adder_1_sum[3]),
    .Cout(n1_bit_ripple_adder_4_cout));
  Counter #(.width(4), .max('hf)) counter_1 (
    .D(n1_bit_ripple_adder_1_sum), .count(n1_bit_ripple_adder_4_cout), .Q(Sum), .carry(Overflow),
    .clk(Clock), .clr(Reset));  // open: load

  // Notes on the sheet:
  //   LSB
  //   MSB
endmodule

module Right_player (
  input  A,
  input  B,
  input  C,
  input  D,
  output Win,
  output Tie,
  output Lose
);

  wire and_1_out, and_2_out, and_3_out, and_4_out, and_5_out, and_6_out, and_7_out, and_8_out, and_9_out,
       not_1_out, not_2_out, not_3_out, not_4_out, not_5_out, not_6_out, not_7_out, not_8_out, not_9_out,
       not_10_out, not_11_out, not_12_out;

  not not_1 (not_1_out, A);
  not not_2 (not_2_out, D);
  not not_3 (not_3_out, B);
  not not_4 (not_4_out, C);
  not not_5 (not_5_out, A);
  not not_6 (not_6_out, C);
  not not_7 (not_7_out, B);
  not not_8 (not_8_out, D);
  not not_9 (not_9_out, A);
  not not_10 (not_10_out, B);
  not not_11 (not_11_out, C);
  not not_12 (not_12_out, D);
  and and_1 (and_1_out, not_1_out, B, C, not_2_out);
  and and_2 (and_2_out, A, not_3_out, C, D);
  or or_1 (Win, and_1_out, and_2_out, and_3_out);
  and and_3 (and_3_out, A, B, not_4_out, D);
  and and_4 (and_4_out, not_5_out, B, not_6_out, D);
  or or_2 (Tie, and_4_out, and_5_out, and_6_out);
  and and_5 (and_5_out, A, not_7_out, C, not_8_out);
  and and_6 (and_6_out, A, B, C, D);
  and and_7 (and_7_out, not_9_out, B, C, D);
  or or_3 (Lose, and_7_out, and_8_out, and_9_out);
  and and_8 (and_8_out, A, not_10_out, not_11_out, D);
  and and_9 (and_9_out, A, B, C, not_12_out);
endmodule

module Left_player (
  input  A,
  input  B,
  input  C,
  input  D,
  output Win,
  output Tie,
  output Lose
);

  wire and_1_out, and_2_out, and_3_out, and_4_out, and_5_out, and_6_out, and_7_out, and_8_out, and_9_out,
       not_1_out, not_2_out, not_3_out, not_4_out, not_5_out, not_6_out, not_7_out, not_8_out, not_9_out,
       not_10_out, not_11_out, not_12_out;

  not not_1 (not_1_out, A);
  not not_2 (not_2_out, B);
  not not_3 (not_3_out, C);
  not not_4 (not_4_out, D);
  not not_5 (not_5_out, A);
  not not_6 (not_6_out, C);
  not not_7 (not_7_out, B);
  not not_8 (not_8_out, D);
  not not_9 (not_9_out, A);
  not not_10 (not_10_out, D);
  not not_11 (not_11_out, B);
  not not_12 (not_12_out, C);
  and and_1 (and_1_out, not_1_out, B, C, D);
  and and_2 (and_2_out, A, not_2_out, not_3_out, D);
  or or_1 (Win, and_1_out, and_2_out, and_3_out);
  and and_3 (and_3_out, A, B, C, not_4_out);
  and and_4 (and_4_out, not_5_out, B, not_6_out, D);
  and and_5 (and_5_out, A, not_7_out, C, not_8_out);
  or or_2 (Tie, and_4_out, and_5_out, and_6_out);
  and and_6 (and_6_out, A, B, C, D);
  and and_7 (and_7_out, not_9_out, B, C, not_10_out);
  and and_8 (and_8_out, A, not_11_out, C, D);
  or or_3 (Lose, and_7_out, and_8_out, and_9_out);
  and and_9 (and_9_out, A, B, not_12_out, D);
endmodule

module Left (
  input  A,
  input  B,
  input  C,
  input  D,
  output win_tie,
  output win
);

  wire and_1_out, and_2_out, and_3_out, and_4_out, and_5_out, and_6_out, and_7_out, not_1_out, not_2_out,
       not_3_out, not_4_out, not_5_out, not_6_out, not_7_out, not_8_out;

  not not_1 (not_1_out, A);
  not not_2 (not_2_out, B);
  not not_3 (not_3_out, C);
  not not_4 (not_4_out, D);
  not not_5 (not_5_out, A);
  not not_6 (not_6_out, B);
  not not_7 (not_7_out, C);
  not not_8 (not_8_out, D);
  and and_1 (and_1_out, not_1_out, B, D);
  and and_2 (and_2_out, B, C, D);
  and and_3 (and_3_out, A, not_2_out, not_3_out, D);
  and and_4 (and_4_out, A, C, not_4_out);
  and and_5 (and_5_out, not_5_out, B, C, D);
  or or_1 (win, and_5_out, and_6_out, and_7_out);
  and and_6 (and_6_out, A, not_6_out, not_7_out, D);
  and and_7 (and_7_out, A, B, C, not_8_out);
  or or_2 (win_tie, and_1_out, and_2_out, and_3_out, and_4_out);
endmodule

module Right (
  input  A,
  input  B,
  input  C,
  input  D,
  output win_tie,
  output win
);

  wire and_1_out, and_2_out, and_3_out, and_4_out, and_5_out, and_6_out, and_7_out, not_1_out, not_2_out,
       not_3_out, not_4_out, not_5_out, not_6_out, not_7_out, not_8_out;

  not not_1 (not_1_out, C);
  not not_2 (not_2_out, A);
  not not_3 (not_3_out, D);
  not not_4 (not_4_out, B);
  not not_5 (not_5_out, A);
  not not_6 (not_6_out, D);
  not not_7 (not_7_out, B);
  not not_8 (not_8_out, C);
  and and_1 (and_1_out, B, not_1_out, D);
  and and_2 (and_2_out, not_2_out, B, C, not_3_out);
  and and_3 (and_3_out, A, not_4_out, C);
  and and_4 (and_4_out, A, B, D);
  and and_5 (and_5_out, not_5_out, B, C, not_6_out);
  and and_6 (and_6_out, A, not_7_out, C, D);
  or or_1 (win, and_5_out, and_6_out, and_7_out);
  and and_7 (and_7_out, A, B, not_8_out, D);
  or or_2 (win_tie, and_1_out, and_2_out, and_3_out, and_4_out);
endmodule

module left_win_tie (
  input  A,
  input  B,
  input  C,
  input  D,
  output win_tie
);

  wire and_1_out, and_2_out, and_3_out, and_4_out, not_1_out, not_2_out, not_3_out, not_4_out;

  not not_1 (not_1_out, A);
  not not_2 (not_2_out, B);
  not not_3 (not_3_out, C);
  not not_4 (not_4_out, D);
  and and_1 (and_1_out, not_1_out, B, D);
  and and_2 (and_2_out, B, C, D);
  and and_3 (and_3_out, A, not_2_out, not_3_out, D);
  and and_4 (and_4_out, A, C, not_4_out);
  or or_1 (win_tie, and_1_out, and_2_out, and_3_out, and_4_out);
endmodule

module left_win (
  input  A,
  input  B,
  input  C,
  input  D,
  output win
);

  wire and_1_out, and_2_out, and_3_out, and_4_out, and_5_out, and_6_out, and_7_out, and_8_out, and_9_out,
       not_1_out, not_2_out, not_3_out, not_4_out, or_1_out;

  not not_1 (not_1_out, A);
  and and_1 (and_1_out, not_1_out, B);
  and and_2 (and_2_out, C, D);
  and and_3 (and_3_out, A, not_2_out);
  not not_2 (not_2_out, B);
  not not_3 (not_3_out, C);
  and and_4 (and_4_out, not_3_out, D);
  not not_4 (not_4_out, D);
  and and_5 (and_5_out, and_1_out, and_2_out);
  and and_6 (and_6_out, and_3_out, and_4_out);
  and and_7 (and_7_out, A, B);
  and and_8 (and_8_out, C, not_4_out);
  or or_1 (or_1_out, and_5_out, and_6_out);
  and and_9 (and_9_out, and_7_out, and_8_out);
  or or_2 (win, or_1_out, and_9_out);
endmodule

module right_win_tie (
  input  A,
  input  B,
  input  C,
  input  D,
  output win_tie
);

  wire and_1_out, and_2_out, and_3_out, and_4_out, not_1_out, not_2_out, not_3_out, not_4_out;

  not not_1 (not_1_out, C);
  not not_2 (not_2_out, A);
  not not_3 (not_3_out, D);
  not not_4 (not_4_out, B);
  and and_1 (and_1_out, B, not_1_out, D);
  and and_2 (and_2_out, not_2_out, B, C, not_3_out);
  and and_3 (and_3_out, A, not_4_out, C);
  and and_4 (and_4_out, A, B, D);
  or or_1 (win_tie, and_1_out, and_2_out, and_3_out, and_4_out);
endmodule

module right_win (
  input  A,
  input  B,
  input  C,
  input  D,
  output win
);

  wire and_1_out, and_2_out, and_3_out, not_1_out, not_2_out, not_3_out, not_4_out;

  not not_1 (not_1_out, A);
  not not_2 (not_2_out, D);
  not not_3 (not_3_out, B);
  not not_4 (not_4_out, C);
  and and_1 (and_1_out, not_1_out, B, C, not_2_out);
  or or_1 (win, and_1_out, and_2_out, and_3_out);
  and and_2 (and_2_out, A, not_3_out, C, D);
  and and_3 (and_3_out, A, B, not_4_out, D);
endmodule

module Left_subcircuit (
  input  A,
  input  B,
  input  reset,
  input  Clock,
  input  C,
  input  D,
  output Win_Tie,
  output Win,
  output Lose,
  output [3:0] Sum
);

  wire left_1_win, left_1_win_tie, not_1_out, not_2_out, right_1_win, right_1_win_tie;
  wire [3:0] bit_extender_1_out;

  Left left_1 (.A(A), .B(B), .C(C), .D(D), .win_tie(left_1_win_tie), .win(left_1_win));
  Right right_1 (.A(A), .B(B), .C(C), .D(D), .win_tie(right_1_win_tie), .win(right_1_win));
  assign bit_extender_1_out = {{3{left_1_win_tie}}, left_1_win};  // Bit_Extender bit_extender_1
  Bit_Extender #(.in_width(1), .out_width(4), .\type ("input")) bit_extender_2 (
    .in(right_1_win), .extend(right_1_win_tie));  // open: out
  and and_1 (Win_Tie, left_1_win_tie, right_1_win_tie);
  not not_1 (not_1_out, right_1_win_tie);
  _4_bit_counter u_4_bit_counter_1 (
    .A(bit_extender_1_out), .B(bit_extender_1_out), .Clock(Clock), .Reset(reset), .Sum(Sum));  // open: Overflow
  and and_2 (Win, left_1_win_tie, not_1_out);
  not not_2 (not_2_out, left_1_win_tie);
  and and_3 (Lose, not_2_out, right_1_win_tie);
endmodule

module Right_subcircuit (
  input  A,
  input  B,
  input  reset,
  input  Clock,
  input  C,
  input  D,
  output Win_Tie,
  output Win,
  output Lose,
  output [3:0] Sum
);

  wire left_1_win, left_1_win_tie, not_1_out, not_2_out, right_1_win, right_1_win_tie;
  wire [3:0] bit_extender_2_out;

  Left left_1 (.A(A), .B(B), .C(C), .D(D), .win_tie(left_1_win_tie), .win(left_1_win));
  Right right_1 (.A(A), .B(B), .C(C), .D(D), .win_tie(right_1_win_tie), .win(right_1_win));
  Bit_Extender #(.in_width(1), .out_width(4), .\type ("input")) bit_extender_1 (
    .in(left_1_win), .extend(left_1_win_tie));  // open: out
  assign bit_extender_2_out = {{3{right_1_win_tie}}, right_1_win};  // Bit_Extender bit_extender_2
  and and_1 (Win_Tie, left_1_win_tie, right_1_win_tie);
  _4_bit_counter u_4_bit_counter_1 (
    .A(bit_extender_2_out), .B(bit_extender_2_out), .Clock(Clock), .Reset(reset), .Sum(Sum));  // open: Overflow
  not not_1 (not_1_out, left_1_win_tie);
  and and_2 (Win, not_1_out, right_1_win_tie);
  not not_2 (not_2_out, right_1_win_tie);
  and and_3 (Lose, left_1_win_tie, not_2_out);
endmodule

module AI_subcircuit (
  input  A,
  input  B,
  input  Reset,
  input  Reset_2,
  output D,
  output C,
  output Tie,
  output Tie_2,
  output Lose,
  output Win,
  output Lose_2,
  output Win_2
);

  wire clock_1_out;
  wire [3:0] left_subcircuit_1_sum, right_subcircuit_1_sum;

  Clock clock_1 (.out(clock_1_out));
  Left_subcircuit left_subcircuit_1 (
    .A(A), .B(B), .C(C), .D(D), .Sum(left_subcircuit_1_sum), .Clock(clock_1_out), .Win_Tie(Tie), .Win(Win),
    .Lose(Lose), .reset(Reset));
  Hex_Digit_Display hex_digit_display_1 (.value(left_subcircuit_1_sum));  // open: dp
  Random #(.width(1)) random_1 (.clk(clock_1_out), .out(C));  // open: next, clr
  Random #(.width(1), .seed(2)) random_2 (.clk(clock_1_out), .out(D));  // open: next, clr
  Right_subcircuit right_subcircuit_1 (
    .A(A), .B(B), .C(C), .D(D), .Sum(right_subcircuit_1_sum), .Clock(clock_1_out), .Win_Tie(Tie_2),
    .Win(Win_2), .Lose(Lose_2), .reset(Reset_2));
  Hex_Digit_Display hex_digit_display_2 (.value(right_subcircuit_1_sum));  // open: dp

  // Notes on the sheet:
  //   Left player
  //   Left player score
  //   Right player
  //   Inputs: 
  //   Rock: 01
  //   Paper: 10
  //   Scissors: 11
  //   Right player score
  //   illegal: 00
endmodule
